// Logisim project CPU.circ as structural Verilog: 10 circuits, main circuit main
module main (
  input  rst,
  output [31:0] out_2,
  output [31:0] out_3,
  output out_4,
  output [4:0] out_5,
  output [31:0] out_6,
  output out_7,
  output [31:0] out_8,
  output [31:0] out_9
);

  wire ALUSrc, branch, clk, equal_sign, EXTOp, MemRead, MemtoReg, PCSrc_out, RegDst;
  wire [3:0] ALUOp;
  wire [31:0] imm_32, multiplexer_3_out, npc, RD1, ReadData;

  Clock u_clk (.out(clk));
  IFU ifu_1 (.in_2(clk), .in_3(rst), .\output (out_2), .npc(npc), .pc(out_3));
  NPC npc_1 (.in_3(imm_32), .PCSrc(PCSrc_out), .pc(out_3), .npc(npc));
  and PCSrc (PCSrc_out, equal_sign, branch);
  Multiplexer #(.width(5), .enable("false")) multiplexer_1 (
    .in0(out_2[20:16]), .in1(out_2[15:11]), .out(out_5), .sel(RegDst));
  Multiplexer #(.width(32), .enable("false")) multiplexer_2 (.in0(out_8), .in1(ReadData), .out(out_6), .sel(MemtoReg));
  Controller controller_1 (
    .funct(out_2[5:0]), .opcode(out_2[31:26]), .out_3(RegDst), .out_4(ALUSrc), .out_5(MemtoReg),
    .out_6(out_4), .out_7(MemRead), .out_8(out_7), .out_9(branch), .ALUOp(ALUOp), .out_11(EXTOp));
  GRF grf_1 (
    .A1(out_2[25:21]), .A2(out_2[20:16]), .A3(out_5), .\input (out_6), .RD1(RD1), .RD2(out_9), .clk(clk),
    .reset(rst), .WE(out_4));
  EXT ext_1 (.in_1(out_2[15:0]), .out_3(imm_32), .EXTOp(EXTOp));
  Multiplexer #(.width(32), .enable("false")) multiplexer_3 (
    .in0(out_9), .in1(imm_32), .out(multiplexer_3_out), .sel(ALUSrc));
  ALU alu_1 (.in_2(RD1), .in_3(multiplexer_3_out), .zero(equal_sign), .result(out_8), .ALUOp(ALUOp));
  DM dm_1 (
    .Address(out_8), .DataWrite(out_9), .MemWrite(out_7), .MemRead(MemRead), .rst(rst), .out_7(ReadData),
    .clk(clk));

  // Other names for the same wires on the sheet: _0 = out_2[0]; funct[5:0] = out_2[5:0]; imm[15:0] = out_2[15:0];
  //   Instr[31:0] = out_2; _1 = out_2[1]; _2 = out_2[2]; _3 = out_2[3]; _4 = out_2[4]; _5 = out_2[5]; _6 = out_2[6];
  //   _7 = out_2[7]; _8 = out_2[8]; _9 = out_2[9]; _10 = out_2[10]; _11 = out_2[11]; rd[4:0] = out_2[15:11];
  //   _12 = out_2[12]; _13 = out_2[13]; _14 = out_2[14]; _15 = out_2[15]; _26 = out_2[26]; opcode[5:0] = out_2[31:26];
  //   _27 = out_2[27]; _28 = out_2[28]; _29 = out_2[29]; _30 = out_2[30]; _31 = out_2[31]; MemAddr[31:0] = out_8;
  //   MemWrite = out_7; pc[31:0] = out_3; RD2[31:0] = out_9; RegAddr[4:0] = out_5; RegData[31:0] = out_6;
  //   RegWrite = out_4; _21 = out_2[21]; rs[4:0] = out_2[25:21]; _22 = out_2[22]; _23 = out_2[23]; _24 = out_2[24];
  //   _25 = out_2[25]; _16 = out_2[16]; rt[4:0] = out_2[20:16]; _17 = out_2[17]; _18 = out_2[18]; _19 = out_2[19];
  //   _20 = out_2[20]
endmodule

// pc
module IFU (
  input  [31:0] npc,
  input  in_2,
  input  in_3,
  output [31:0] pc,
  output [31:0] \output 
);

  wire comparator_1_eq;
  wire [11:0] bit_extender_1_out;
  wire [31:0] PC_q, shifter_1_out, subtractor_1_out;

  Register #(.width(32)) u_PC (.D(npc), .Q(PC_q), .clk(in_2), .clr(in_3));  // open: en
  Comparator #(.width(32), .mode("unsigned")) comparator_1 (
    .a(PC_q), .b({32{1'b0}}), .eq(comparator_1_eq));  // open: gt, lt
  Multiplexer #(.width(32), .enable("false")) multiplexer_1 (
    .in0(PC_q), .in1(32'h3000), .out(pc), .sel(comparator_1_eq));
  Subtractor #(.width(32)) subtractor_1 (.a(pc), .b(32'h3000), .out(subtractor_1_out));  // open: bin, bout
  Shifter #(.width(32), .shift("lr")) shifter_1 (.in(subtractor_1_out), .\dist (5'b00010), .out(shifter_1_out));
  Bit_Extender #(.in_width(32), .out_width(12)) bit_extender_1 (.in(shifter_1_out), .out(bit_extender_1_out));
  ROM #(.addrWidth(12), .dataWidth(32)) rom_1 (.addr(bit_extender_1_out), .data(\output ));  // open: sel

  // Other names for the same wires on the sheet: clk = in_2; rst = in_3

  // Notes on the sheet:
  //   contents of rom_1 (hex, n*v repeats v):
  //   8c83ffff
endmodule

module NPC (
  input  [31:0] pc,
  input  PCSrc,
  input  [31:0] in_3,
  output [31:0] npc
);

  wire [31:0] adder_1_out, adder_2_out, shifter_1_out;

  Shifter #(.width(32)) shifter_1 (.in(in_3), .\dist (5'b00010), .out(shifter_1_out));
  Adder #(.width(32)) adder_1 (.a(pc), .b(32'h4), .out(adder_1_out));  // open: cin, cout
  Adder #(.width(32)) adder_2 (.a(adder_1_out), .b(shifter_1_out), .out(adder_2_out));  // open: cin, cout
  Multiplexer #(.width(32), .enable("false")) multiplexer_1 (
    .in0(adder_1_out), .in1(adder_2_out), .out(npc), .sel(PCSrc));
endmodule

module GRF (
  input  reset,
  input  clk,
  input  WE,
  input  [4:0] A1,
  input  [4:0] A2,
  input  [4:0] A3,
  input  [31:0] \input ,
  output [31:0] RD1,
  output [31:0] RD2
);

  wire [31:0] _0, _1, _2, _3, _4, _5, _6, _7, _8, _9, _10, _11, _12, _13, _14, _15, _16, _17, _18, _19, _20,
       _21, _22, _23, _24, _25, _26, _27, _28, _29, _30, _31, O0, O1, O2, O3, O4, O5, O6, O7, O8, O9, O10,
       O11, O12, O13, O14, O15, O16, O17, O18, O19, O20, O21, O22, O23, O24, O25, O26, O27, O28, O29, O30,
       O31;

  Demultiplexer #(.select(5), .width(32), .tristate("true")) demultiplexer_1 (
    .out0(_0), .out1(_1), .out2(_2), .out3(_3), .out4(_4), .out5(_5), .out6(_6), .out7(_7), .out8(_8),
    .out9(_9), .out10(_10), .out11(_11), .out12(_12), .out13(_13), .out14(_14), .out15(_15), .out16(_16),
    .out17(_17), .out18(_18), .out19(_19), .out20(_20), .out21(_21), .out22(_22), .out23(_23), .out24(_24),
    .out25(_25), .out26(_26), .out27(_27), .out28(_28), .out29(_29), .out30(_30), .out31(_31), .in(\input ),
    .sel(A3), .en(WE));
  Register #(.width(32)) register_1 (.D(_0), .en(1'b0), .Q(O0), .clk(clk), .clr(reset));
  Register #(.width(32)) register_2 (.D(_4), .en(WE), .Q(O4), .clk(clk), .clr(reset));
  Register #(.width(32)) register_3 (.D(_8), .en(WE), .Q(O8), .clk(clk), .clr(reset));
  Register #(.width(32)) register_4 (.D(_12), .en(WE), .Q(O12), .clk(clk), .clr(reset));
  Register #(.width(32)) register_5 (.D(_16), .en(WE), .Q(O16), .clk(clk), .clr(reset));
  Register #(.width(32)) register_6 (.D(_20), .en(WE), .Q(O20), .clk(clk), .clr(reset));
  Register #(.width(32)) register_7 (.D(_24), .en(WE), .Q(O24), .clk(clk), .clr(reset));
  Register #(.width(32)) register_8 (.D(_28), .en(WE), .Q(O28), .clk(clk), .clr(reset));
  Register #(.width(32)) register_9 (.D(_1), .en(WE), .Q(O1), .clk(clk), .clr(reset));
  Register #(.width(32)) register_10 (.D(_5), .en(WE), .Q(O5), .clk(clk), .clr(reset));
  Register #(.width(32)) register_11 (.D(_9), .en(WE), .Q(O9), .clk(clk), .clr(reset));
  Register #(.width(32)) register_12 (.D(_13), .en(WE), .Q(O13), .clk(clk), .clr(reset));
  Register #(.width(32)) register_13 (.D(_17), .en(WE), .Q(O17), .clk(clk), .clr(reset));
  Register #(.width(32)) register_14 (.D(_21), .en(WE), .Q(O21), .clk(clk), .clr(reset));
  Register #(.width(32)) register_15 (.D(_25), .en(WE), .Q(O25), .clk(clk), .clr(reset));
  Register #(.width(32)) register_16 (.D(_29), .en(WE), .Q(O29), .clk(clk), .clr(reset));
  Register #(.width(32)) register_17 (.D(_2), .en(WE), .Q(O2), .clk(clk), .clr(reset));
  Register #(.width(32)) register_18 (.D(_6), .en(WE), .Q(O6), .clk(clk), .clr(reset));
  Register #(.width(32)) register_19 (.D(_10), .en(WE), .Q(O10), .clk(clk), .clr(reset));
  Register #(.width(32)) register_20 (.D(_14), .en(WE), .Q(O14), .clk(clk), .clr(reset));
  Register #(.width(32)) register_21 (.D(_18), .en(WE), .Q(O18), .clk(clk), .clr(reset));
  Register #(.width(32)) register_22 (.D(_22), .en(WE), .Q(O22), .clk(clk), .clr(reset));
  Register #(.width(32)) register_23 (.D(_26), .en(WE), .Q(O26), .clk(clk), .clr(reset));
  Register #(.width(32)) register_24 (.D(_30), .en(WE), .Q(O30), .clk(clk), .clr(reset));
  Register #(.width(32)) register_25 (.D(_3), .en(WE), .Q(O3), .clk(clk), .clr(reset));
  Register #(.width(32)) register_26 (.D(_7), .en(WE), .Q(O7), .clk(clk), .clr(reset));
  Register #(.width(32)) register_27 (.D(_11), .en(WE), .Q(O11), .clk(clk), .clr(reset));
  Register #(.width(32)) register_28 (.D(_15), .en(WE), .Q(O15), .clk(clk), .clr(reset));
  Register #(.width(32)) register_29 (.D(_19), .en(WE), .Q(O19), .clk(clk), .clr(reset));
  Register #(.width(32)) register_30 (.D(_23), .en(WE), .Q(O23), .clk(clk), .clr(reset));
  Register #(.width(32)) register_31 (.D(_27), .en(WE), .Q(O27), .clk(clk), .clr(reset));
  Register #(.width(32)) register_32 (.D(_31), .en(WE), .Q(O31), .clk(clk), .clr(reset));
  Multiplexer #(.select(5), .width(32), .enable("false")) multiplexer_1 (
    .in0(O0), .in1(O1), .in2(O2), .in3(O3), .in4(O4), .in5(O5), .in6(O6), .in7(O7), .in8(O8), .in9(O9),
    .in10(O10), .in11(O11), .in12(O12), .in13(O13), .in14(O14), .in15(O15), .in16(O16), .in17(O17),
    .in18(O18), .in19(O19), .in20(O20), .in21(O21), .in22(O22), .in23(O23), .in24(O24), .in25(O25),
    .in26(O26), .in27(O27), .in28(O28), .in29(O29), .in30(O30), .in31(O31), .out(RD2), .sel(A2));
  Multiplexer #(.select(5), .width(32)) multiplexer_2 (
    .in0(O0), .in1(O1), .in2(O2), .in3(O3), .in4(O4), .in5(O5), .in6(O6), .in7(O7), .in8(O8), .in9(O9),
    .in10(O10), .in11(O11), .in12(O12), .in13(O13), .in14(O14), .in15(O15), .in16(O16), .in17(O17),
    .in18(O18), .in19(O19), .in20(O20), .in21(O21), .in22(O22), .in23(O23), .in24(O24), .in25(O25),
    .in26(O26), .in27(O27), .in28(O28), .in29(O29), .in30(O30), .in31(O31), .out(RD1), .sel(A1));  // open: en
endmodule

module ALU (
  input  [3:0] ALUOp,
  input  [31:0] in_2,
  input  [31:0] in_3,
  output zero,
  output [31:0] result
);

  wire [15:0] bit_extender_1_out;
  wire [31:0] adder_1_out, address_prime, and_1_out, imm_32_prime, or_1_out, subtractor_1_out,
       subtractor_2_out, subtractor_3_out, subtractor_4_out;

  Bit_Extender #(.in_width(32)) bit_extender_1 (.in(in_3), .out(bit_extender_1_out));
  Subtractor #(.width(32)) subtractor_1 (.a(in_2), .b(imm_32_prime), .out(subtractor_1_out));  // open: bin, bout
  assign and_1_out = in_2 & in_3;  // AND_Gate and_1, 32 bits wide
  assign or_1_out = in_2 | in_3;  // OR_Gate or_1, 32 bits wide
  Adder #(.width(32)) adder_1 (.a(in_2), .b(in_3), .out(adder_1_out));  // open: cin, cout
  Subtractor #(.width(32)) subtractor_2 (.a(in_2), .b(in_3), .out(subtractor_2_out));  // open: bin, bout
  Comparator #(.width(32), .mode("unsigned")) comparator_1 (
    .a(subtractor_2_out), .b({32{1'b0}}), .eq(zero));  // open: gt, lt
  Multiplexer #(.select(4), .width(32), .enable("false")) multiplexer_1 (
    .in0(and_1_out), .in1(or_1_out), .in2(adder_1_out), .in6(subtractor_2_out),
    .in8({bit_extender_1_out, {16{1'b0}}}), .out(result), .sel(ALUOp));  // open: in3, in4, in5, in7, in9, in10, in11, in12, in13, in14, in15
  Subtractor #(.width(32)) subtractor_3 (.a(in_3), .b(32'h1), .out(subtractor_3_out));  // open: bin, bout
  Subtractor #(.width(32)) subtractor_4 (.a(in_2), .b(32'h1), .out(subtractor_4_out));  // open: bin, bout
  not not_1 (imm_32_prime[0], subtractor_3_out[0]);
  not not_2 (imm_32_prime[1], subtractor_3_out[1]);
  not not_3 (imm_32_prime[2], subtractor_3_out[2]);
  not not_4 (imm_32_prime[3], subtractor_3_out[3]);
  not not_5 (imm_32_prime[4], subtractor_3_out[4]);
  not not_6 (imm_32_prime[5], subtractor_3_out[5]);
  not not_7 (imm_32_prime[6], subtractor_3_out[6]);
  not not_8 (imm_32_prime[7], subtractor_3_out[7]);
  not not_9 (imm_32_prime[8], subtractor_3_out[8]);
  not not_10 (imm_32_prime[9], subtractor_3_out[9]);
  not not_11 (imm_32_prime[10], subtractor_3_out[10]);
  not not_12 (imm_32_prime[11], subtractor_3_out[11]);
  not not_13 (imm_32_prime[12], subtractor_3_out[12]);
  not not_14 (imm_32_prime[13], subtractor_3_out[13]);
  not not_15 (imm_32_prime[14], subtractor_3_out[14]);
  not not_16 (imm_32_prime[15], subtractor_3_out[15]);
  not not_17 (imm_32_prime[16], subtractor_3_out[16]);
  not not_18 (imm_32_prime[17], subtractor_3_out[17]);
  not not_19 (imm_32_prime[18], subtractor_3_out[18]);
  not not_20 (imm_32_prime[19], subtractor_3_out[19]);
  not not_21 (imm_32_prime[20], subtractor_3_out[20]);
  not not_22 (imm_32_prime[21], subtractor_3_out[21]);
  not not_23 (imm_32_prime[22], subtractor_3_out[22]);
  not not_24 (imm_32_prime[23], subtractor_3_out[23]);
  not not_25 (imm_32_prime[24], subtractor_3_out[24]);
  not not_26 (imm_32_prime[25], subtractor_3_out[25]);
  not not_27 (imm_32_prime[26], subtractor_3_out[26]);
  not not_28 (imm_32_prime[27], subtractor_3_out[27]);
  not not_29 (imm_32_prime[28], subtractor_3_out[28]);
  not not_30 (imm_32_prime[29], subtractor_3_out[29]);
  not not_31 (imm_32_prime[30], subtractor_3_out[30]);
  not not_32 (imm_32_prime[31], subtractor_3_out[31]);
  not not_33 (address_prime[0], subtractor_4_out[0]);
  not not_34 (address_prime[1], subtractor_4_out[1]);
  not not_35 (address_prime[2], subtractor_4_out[2]);
  not not_36 (address_prime[3], subtractor_4_out[3]);
  not not_37 (address_prime[4], subtractor_4_out[4]);
  not not_38 (address_prime[5], subtractor_4_out[5]);
  not not_39 (address_prime[6], subtractor_4_out[6]);
  not not_40 (address_prime[7], subtractor_4_out[7]);
  not not_41 (address_prime[8], subtractor_4_out[8]);
  not not_42 (address_prime[9], subtractor_4_out[9]);
  not not_43 (address_prime[10], subtractor_4_out[10]);
  not not_44 (address_prime[11], subtractor_4_out[11]);
  not not_45 (address_prime[12], subtractor_4_out[12]);
  not not_46 (address_prime[13], subtractor_4_out[13]);
  not not_47 (address_prime[14], subtractor_4_out[14]);
  not not_48 (address_prime[15], subtractor_4_out[15]);
  not not_49 (address_prime[16], subtractor_4_out[16]);
  not not_50 (address_prime[17], subtractor_4_out[17]);
  not not_51 (address_prime[18], subtractor_4_out[18]);
  not not_52 (address_prime[19], subtractor_4_out[19]);
  not not_53 (address_prime[20], subtractor_4_out[20]);
  not not_54 (address_prime[21], subtractor_4_out[21]);
  not not_55 (address_prime[22], subtractor_4_out[22]);
  not not_56 (address_prime[23], subtractor_4_out[23]);
  not not_57 (address_prime[24], subtractor_4_out[24]);
  not not_58 (address_prime[25], subtractor_4_out[25]);
  not not_59 (address_prime[26], subtractor_4_out[26]);
  not not_60 (address_prime[27], subtractor_4_out[27]);
  not not_61 (address_prime[28], subtractor_4_out[28]);
  not not_62 (address_prime[29], subtractor_4_out[29]);
  not not_63 (address_prime[30], subtractor_4_out[30]);
  not not_64 (address_prime[31], subtractor_4_out[31]);

  // Other names for the same wires on the sheet: address[31:0] = in_2; sign1 = in_2[31]; imm_32[31:0] = in_3;
  //   sign2 = in_3[31]; OP[3:0] = ALUOp
endmodule

module Controller_AND_logic (
  input  func5,
  input  func4,
  input  func3,
  input  func2,
  input  func1,
  input  func0,
  input  op5,
  input  op4,
  input  op3,
  input  op2,
  input  op1,
  input  op0,
  output out_13,
  output out_14,
  output out_15,
  output out_16,
  output out_17,
  output out_18,
  output out_19
);

  wire R_out;
  wire [15:0] not_5_out, not_12_out;

  not not_1 (not_5_out[15], op5);
  not not_2 (not_5_out[12], op4);
  not not_3 (not_5_out[9], op3);
  not not_4 (not_5_out[6], op2);
  not not_5 (not_5_out[0], op0);
  not not_6 (not_5_out[3], op1);
  and ori (out_13, not_5_out[15], not_5_out[12], op3, op2, not_5_out[3], op0);
  and lw (out_14, op5, not_5_out[12], not_5_out[9], not_5_out[6], op1, op0);
  and sw (out_15, op5, not_5_out[12], op3, not_5_out[6], op1, op0);
  and beq (out_16, not_5_out[15], not_5_out[12], not_5_out[9], op2, not_5_out[3], not_5_out[0]);
  and lui (out_17, not_5_out[15], not_5_out[12], op3, op2, op1, op0);
  and R (R_out, not_5_out[15], not_5_out[12], not_5_out[9], not_5_out[6], not_5_out[3], not_5_out[0]);
  not not_7 (not_12_out[15], func5);
  not not_8 (not_12_out[12], func4);
  not not_9 (not_12_out[6], func2);
  not not_10 (not_12_out[9], func3);
  not not_11 (not_12_out[3], func1);
  not not_12 (not_12_out[0], func0);
  and add (out_18, R_out, func5, not_12_out[12], not_12_out[9], not_12_out[6], not_12_out[3], not_12_out[0]);
  and sub (out_19, R_out, func5, not_12_out[12], not_12_out[9], not_12_out[6], func1, not_12_out[0]);
endmodule

// lw
module Controller_OR_logic (
  input  ori,
  input  lw,
  input  sw,
  input  beq,
  input  lui,
  input  add,
  input  sub,
  output out_8,
  output out_9,
  output out_10,
  output out_11,
  output out_12,
  output out_13,
  output out_14,
  output out_15,
  output out_16,
  output out_17,
  output out_18,
  output out_19
);

  or RegDst (out_8, add, sub);
  or ALUSrc (out_9, lw, sw, ori, lui);
  buf MemtoReg (out_10, lw);  // OR_Gate
  or RegWrite (out_11, add, sub, lw, ori, lui);
  buf MemRead (out_12, lw);  // OR_Gate
  buf MemWrite (out_13, sw);  // OR_Gate
  buf branch (out_14, beq);  // OR_Gate
  buf ALUOp3 (out_15, lui);  // OR_Gate
  or ALUOp2 (out_16, sub, beq);
  or ALUOp1 (out_17, add, sub, lw, sw, beq);
  buf ALUOp0 (out_18, ori);  // OR_Gate
  or EXTOp (out_19, beq, sw, lw);
endmodule

module Controller (
  input  [5:0] funct,
  input  [5:0] opcode,
  output out_3,
  output out_4,
  output out_5,
  output out_6,
  output out_7,
  output out_8,
  output out_9,
  output [3:0] ALUOp,
  output out_11
);

  wire controller_and_logic_1_out_13, controller_and_logic_1_out_14, controller_and_logic_1_out_15,
       controller_and_logic_1_out_16, controller_and_logic_1_out_17, controller_and_logic_1_out_18,
       controller_and_logic_1_out_19;

  Controller_AND_logic controller_and_logic_1 (
    .out_13(controller_and_logic_1_out_13), .out_14(controller_and_logic_1_out_14),
    .out_15(controller_and_logic_1_out_15), .out_16(controller_and_logic_1_out_16),
    .out_17(controller_and_logic_1_out_17), .out_18(controller_and_logic_1_out_18),
    .out_19(controller_and_logic_1_out_19), .op5(opcode[5]), .op4(opcode[4]), .op3(opcode[3]),
    .op2(opcode[2]), .op1(opcode[1]), .op0(opcode[0]), .func5(funct[5]), .func4(funct[4]), .func3(funct[3]),
    .func2(funct[2]), .func1(funct[1]), .func0(funct[0]));
  Controller_OR_logic controller_or_logic_1 (
    .ori(controller_and_logic_1_out_13), .lw(controller_and_logic_1_out_14),
    .sw(controller_and_logic_1_out_15), .beq(controller_and_logic_1_out_16),
    .lui(controller_and_logic_1_out_17), .add(controller_and_logic_1_out_18),
    .sub(controller_and_logic_1_out_19), .out_8(out_3), .out_9(out_4), .out_10(out_5), .out_11(out_6),
    .out_12(out_7), .out_13(out_8), .out_14(out_9), .out_15(ALUOp[3]), .out_16(ALUOp[2]), .out_17(ALUOp[1]),
    .out_18(ALUOp[0]), .out_19(out_11));

  // Other names for the same wires on the sheet: ALUSrc = out_4; branch = out_9; EXTOp = out_11; MemRead = out_7;
  //   MemtoReg = out_5; MemWrite = out_8; RegDst = out_3; RegWrite = out_6
endmodule

module EXT (
  input  [15:0] in_1,
  input  EXTOp,
  output [31:0] out_3
);

  wire [31:0] bit_extender_1_out, bit_extender_2_out;

  assign bit_extender_1_out = {{16{1'b0}}, in_1};  // Bit_Extender bit_extender_1
  assign bit_extender_2_out = {{16{in_1[15]}}, in_1};  // Bit_Extender bit_extender_2
  Multiplexer #(.width(32), .enable("false")) multiplexer_1 (
    .in0(bit_extender_1_out), .in1(bit_extender_2_out), .out(out_3), .sel(EXTOp));
endmodule

module DM (
  input  [31:0] Address,
  input  [31:0] DataWrite,
  input  clk,
  input  rst,
  input  MemWrite,
  input  MemRead,
  output [31:0] out_7
);

  wire [11:0] bit_extender_1_out;
  wire [31:0] shifter_1_out;

  Shifter #(.width(32), .shift("lr")) shifter_1 (.in(Address), .\dist (5'b00010), .out(shifter_1_out));
  Bit_Extender #(.in_width(32), .out_width(12)) bit_extender_1 (.in(shifter_1_out), .out(bit_extender_1_out));
  RAM #(.addrWidth(12), .dataWidth(32), .bus("separate")) ram_1 (
    .addr(bit_extender_1_out), .din(DataWrite), .data(out_7), .str(MemWrite), .clk(clk), .ld(MemRead),
    .clr(rst));  // open: sel
endmodule
