// Logisim project CRC.circ as structural Verilog: 2 circuits, main circuit CRC
module CRC (
  input  [7:0] input1,
  input  [3:0] input2,
  output [10:0] out_3
);

  wire [2:0] n4_substracter_1_out_3, n4_substracter_2_out_3, n4_substracter_3_out_3, n4_substracter_4_out_3,
       n4_substracter_5_out_3, n4_substracter_6_out_3, n4_substracter_7_out_3;

  _4_substracter u_4_substracter_1 (.A(input1[7:4]), .B(input2), .out_3(n4_substracter_1_out_3));
  _4_substracter u_4_substracter_2 (
    .A({n4_substracter_1_out_3, input1[3]}), .B(input2), .out_3(n4_substracter_2_out_3));
  _4_substracter u_4_substracter_3 (
    .A({n4_substracter_2_out_3, input1[2]}), .B(input2), .out_3(n4_substracter_3_out_3));
  _4_substracter u_4_substracter_4 (
    .A({n4_substracter_3_out_3, input1[1]}), .B(input2), .out_3(n4_substracter_4_out_3));
  _4_substracter u_4_substracter_5 (
    .A({n4_substracter_4_out_3, input1[0]}), .B(input2), .out_3(n4_substracter_5_out_3));
  _4_substracter u_4_substracter_6 (.A({n4_substracter_5_out_3, 1'b0}), .B(input2), .out_3(n4_substracter_6_out_3));
  _4_substracter u_4_substracter_7 (.A({n4_substracter_6_out_3, 1'b0}), .B(input2), .out_3(n4_substracter_7_out_3));
  _4_substracter u_4_substracter_8 (.A({n4_substracter_7_out_3, 1'b0}), .B(input2), .out_3(out_3[2:0]));

  assign out_3[10:3] = input1;
endmodule

module _4_substracter (
  input  [3:0] A,
  input  [3:0] B,
  output [2:0] out_3
);

  wire [2:0] bit_extender_1_out;
  wire [3:0] xor_1_out;

  assign xor_1_out = A ^ B;  // XOR_Gate xor_1, 4 bits wide
  Bit_Extender #(.in_width(4), .out_width(3)) bit_extender_1 (.in(xor_1_out), .out(bit_extender_1_out));
  Multiplexer #(.width(3), .enable("false")) multiplexer_1 (
    .in0(A[2:0]), .in1(bit_extender_1_out), .out(out_3), .sel(A[3]));
endmodule
