// Logisim project GRF.circ as structural Verilog: 1 circuit, main circuit grf
module grf (
  input  reset,
  input  clk,
  input  WE,
  input  [4:0] A1,
  input  [4:0] A2,
  input  [4:0] A3,
  input  [31:0] \input ,
  output [31:0] RD1,
  output [31:0] RD2
);

  wire [31:0] _0, _1, _2, _3, _4, _5, _6, _7, _8, _9, _10, _11, _12, _13, _14, _15, _16, _17, _18, _19, _20,
       _21, _22, _23, _24, _25, _26, _27, _28, _29, _30, _31, O0, O1, O2, O3, O4, O5, O6, O7, O8, O9, O10,
       O11, O12, O13, O14, O15, O16, O17, O18, O19, O20, O21, O22, O23, O24, O25, O26, O27, O28, O29, O30,
       O31;

  Demultiplexer #(.select(5), .width(32), .tristate("true")) demultiplexer_1 (
    .out0(_0), .out1(_1), .out2(_2), .out3(_3), .out4(_4), .out5(_5), .out6(_6), .out7(_7), .out8(_8),
    .out9(_9), .out10(_10), .out11(_11), .out12(_12), .out13(_13), .out14(_14), .out15(_15), .out16(_16),
    .out17(_17), .out18(_18), .out19(_19), .out20(_20), .out21(_21), .out22(_22), .out23(_23), .out24(_24),
    .out25(_25), .out26(_26), .out27(_27), .out28(_28), .out29(_29), .out30(_30), .out31(_31), .in(\input ),
    .sel(A3), .en(WE));
  Register #(.width(32)) register_1 (.D(_0), .en(1'b0), .Q(O0), .clk(clk), .clr(reset));
  Register #(.width(32)) register_2 (.D(_4), .en(WE), .Q(O4), .clk(clk), .clr(reset));
  Register #(.width(32)) register_3 (.D(_8), .en(WE), .Q(O8), .clk(clk), .clr(reset));
  Register #(.width(32)) register_4 (.D(_12), .en(WE), .Q(O12), .clk(clk), .clr(reset));
  Register #(.width(32)) register_5 (.D(_16), .en(WE), .Q(O16), .clk(clk), .clr(reset));
  Register #(.width(32)) register_6 (.D(_20), .en(WE), .Q(O20), .clk(clk), .clr(reset));
  Register #(.width(32)) register_7 (.D(_24), .en(WE), .Q(O24), .clk(clk), .clr(reset));
  Register #(.width(32)) register_8 (.D(_28), .en(WE), .Q(O28), .clk(clk), .clr(reset));
  Register #(.width(32)) register_9 (.D(_1), .en(WE), .Q(O1), .clk(clk), .clr(reset));
  Register #(.width(32)) register_10 (.D(_5), .en(WE), .Q(O5), .clk(clk), .clr(reset));
  Register #(.width(32)) register_11 (.D(_9), .en(WE), .Q(O9), .clk(clk), .clr(reset));
  Register #(.width(32)) register_12 (.D(_13), .en(WE), .Q(O13), .clk(clk), .clr(reset));
  Register #(.width(32)) register_13 (.D(_17), .en(WE), .Q(O17), .clk(clk), .clr(reset));
  Register #(.width(32)) register_14 (.D(_21), .en(WE), .Q(O21), .clk(clk), .clr(reset));
  Register #(.width(32)) register_15 (.D(_25), .en(WE), .Q(O25), .clk(clk), .clr(reset));
  Register #(.width(32)) register_16 (.D(_29), .en(WE), .Q(O29), .clk(clk), .clr(reset));
  Register #(.width(32)) register_17 (.D(_2), .en(WE), .Q(O2), .clk(clk), .clr(reset));
  Register #(.width(32)) register_18 (.D(_6), .en(WE), .Q(O6), .clk(clk), .clr(reset));
  Register #(.width(32)) register_19 (.D(_10), .en(WE), .Q(O10), .clk(clk), .clr(reset));
  Register #(.width(32)) register_20 (.D(_14), .en(WE), .Q(O14), .clk(clk), .clr(reset));
  Register #(.width(32)) register_21 (.D(_18), .en(WE), .Q(O18), .clk(clk), .clr(reset));
  Register #(.width(32)) register_22 (.D(_22), .en(WE), .Q(O22), .clk(clk), .clr(reset));
  Register #(.width(32)) register_23 (.D(_26), .en(WE), .Q(O26), .clk(clk), .clr(reset));
  Register #(.width(32)) register_24 (.D(_30), .en(WE), .Q(O30), .clk(clk), .clr(reset));
  Register #(.width(32)) register_25 (.D(_3), .en(WE), .Q(O3), .clk(clk), .clr(reset));
  Register #(.width(32)) register_26 (.D(_7), .en(WE), .Q(O7), .clk(clk), .clr(reset));
  Register #(.width(32)) register_27 (.D(_11), .en(WE), .Q(O11), .clk(clk), .clr(reset));
  Register #(.width(32)) register_28 (.D(_15), .en(WE), .Q(O15), .clk(clk), .clr(reset));
  Register #(.width(32)) register_29 (.D(_19), .en(WE), .Q(O19), .clk(clk), .clr(reset));
  Register #(.width(32)) register_30 (.D(_23), .en(WE), .Q(O23), .clk(clk), .clr(reset));
  Register #(.width(32)) register_31 (.D(_27), .en(WE), .Q(O27), .clk(clk), .clr(reset));
  Register #(.width(32)) register_32 (.D(_31), .en(WE), .Q(O31), .clk(clk), .clr(reset));
  Multiplexer #(.select(5), .width(32), .enable("false")) multiplexer_1 (
    .in0(O0), .in1(O1), .in2(O2), .in3(O3), .in4(O4), .in5(O5), .in6(O6), .in7(O7), .in8(O8), .in9(O9),
    .in10(O10), .in11(O11), .in12(O12), .in13(O13), .in14(O14), .in15(O15), .in16(O16), .in17(O17),
    .in18(O18), .in19(O19), .in20(O20), .in21(O21), .in22(O22), .in23(O23), .in24(O24), .in25(O25),
    .in26(O26), .in27(O27), .in28(O28), .in29(O29), .in30(O30), .in31(O31), .out(RD2), .sel(A2));
  Multiplexer #(.select(5), .width(32)) multiplexer_2 (
    .in0(O0), .in1(O1), .in2(O2), .in3(O3), .in4(O4), .in5(O5), .in6(O6), .in7(O7), .in8(O8), .in9(O9),
    .in10(O10), .in11(O11), .in12(O12), .in13(O13), .in14(O14), .in15(O15), .in16(O16), .in17(O17),
    .in18(O18), .in19(O19), .in20(O20), .in21(O21), .in22(O22), .in23(O23), .in24(O24), .in25(O25),
    .in26(O26), .in27(O27), .in28(O28), .in29(O29), .in30(O30), .in31(O31), .out(RD1), .sel(A1));  // open: en
endmodule
