// Logisim project FSM.circ as structural Verilog: 3 circuits, main circuit fsm
module fsm (
  input  clr,
  input  [1:0] in,
  output \output 
);

  wire clock_1_out;
  wire [1:0] register_1_q, status_1_status_2;

  status status_1 (.clr(clr), .status(register_1_q), .in(in), .status_2(status_1_status_2));
  Register #(.width(2)) register_1 (.D(status_1_status_2), .Q(register_1_q), .clk(clock_1_out));  // open: en, clr
  Clock clock_1 (.out(clock_1_out));
  \output  output_1 (.status(register_1_q), .in(in), .o(\output ));
endmodule

module status (
  input  clr,
  input  [1:0] status,
  input  [1:0] in,
  output [1:0] status_2
);

  wire and_1_out, and_2_out, and_3_out, and_4_out, not_1_out, not_2_out, not_3_out, not_4_out, not_5_out,
       not_6_out, not_7_out, not_8_out, not_9_out;

  not not_1 (not_1_out, clr);
  not not_2 (not_2_out, status[1]);
  not not_3 (not_3_out, in[0]);
  not not_4 (not_4_out, clr);
  not not_5 (not_5_out, status[0]);
  not not_6 (not_6_out, in[0]);
  not not_7 (not_7_out, clr);
  and and_1 (and_1_out, not_7_out, in[0]);
  not not_8 (not_8_out, clr);
  and and_2 (and_2_out, not_8_out, status[1], not_9_out);
  not not_9 (not_9_out, status[0]);
  and and_3 (and_3_out, not_1_out, not_2_out, status[0], not_3_out);
  or or_1 (status_2[1], and_3_out, and_4_out);
  and and_4 (and_4_out, not_4_out, status[1], not_5_out, not_6_out);
  or or_2 (status_2[0], and_1_out, and_2_out);
endmodule

module \output  (
  input  [1:0] status,
  input  [1:0] in,
  output o
);

  wire not_1_out, not_2_out;

  not not_1 (not_1_out, status[0]);
  not not_2 (not_2_out, in[0]);
  and and_1 (o, status[1], not_1_out, not_2_out);
endmodule
