// Logisim project CPU.circ as structural Verilog: 11 circuits, main circuit main
// signExt
module main (
  input  rst,
  output [31:0] out_2,
  output [31:0] out_3,
  output out_4,
  output [4:0] out_5,
  output [31:0] out_6,
  output out_7,
  output [31:0] out_8,
  output [31:0] out_9
);

  wire ALUSrc, b_or_h, branch, clk, equal_sign, EXTOp, if_branch, JR, judge, jump, MemRead, MemtoReg,
       not_word, overflow, PC_4, ralink, RegDst, shiftvar, signExt, syscall;
  wire [2:0] branchOp;
  wire [3:0] ALUOp;
  wire [4:0] multiplexer_1_out, multiplexer_5_out, rd, rs, rt, shamt;
  wire [5:0] funct, opcode;
  wire [15:0] imm;
  wire [25:0] j_address;
  wire [31:0] imm_32, multiplexer_2_out, multiplexer_6_out, npc, pc_4_t, RD1, ReadData;

  Clock u_clk (.out(clk));
  IFU ifu_1 (.in_2(clk), .in_3(rst), .\output (out_2), .npc(npc), .pc(out_3));
  NPC npc_1 (
    .offset(imm_32), .branch(if_branch), .pc(out_3), .npc(npc), .pc_4(pc_4_t), .jump(jump),
    .reg_address(RD1), .J_address(j_address), .jr(JR));
  InstructionSplitter instructionsplitter_1 (
    .in_1(out_2), .opcode(opcode), .rs(rs), .rt(rt), .rd(rd), .shamt(shamt), .funct(funct), .imm(imm),
    .address(j_address));
  EXT ext_1 (.in_1(imm), .out_3(imm_32), .EXTOp(EXTOp));
  Multiplexer #(.width(5), .enable("false")) multiplexer_1 (.in0(rt), .in1(rd), .out(multiplexer_1_out), .sel(RegDst));
  Multiplexer #(.width(32), .enable("false")) multiplexer_2 (
    .in0(out_8), .in1(ReadData), .out(multiplexer_2_out), .sel(MemtoReg));
  Controller controller_1 (
    .opcode(opcode), .funct(funct), .out_9(RegDst), .out_10(ALUSrc), .out_11(MemtoReg), .out_12(out_4),
    .out_13(MemRead), .out_14(out_7), .out_3(branch), .out_22(ALUOp), .out_4(EXTOp), .out_5(judge),
    .out_7(not_word), .out_8(b_or_h), .out_15(signExt), .out_16(jump), .out_17(JR), .out_18(shiftvar),
    .out_19(ralink), .out_20(PC_4), .out_21(branchOp), .out_6(syscall));
  Multiplexer #(.width(5), .enable("false")) multiplexer_3 (
    .in0(multiplexer_1_out), .in1({5{1'b1}}), .out(out_5), .sel(ralink));
  Multiplexer #(.width(32), .enable("false")) multiplexer_4 (
    .in0(multiplexer_2_out), .in1(pc_4_t), .out(out_6), .sel(PC_4));
  GRF grf_1 (.A1(rs), .A2(rt), .A3(out_5), .\input (out_6), .RD1(RD1), .RD2(out_9), .clk(clk), .reset(rst), .WE(out_4));
  Multiplexer #(.width(5), .enable("false")) multiplexer_5 (
    .in0(shamt), .in1(RD1[4:0]), .out(multiplexer_5_out), .sel(shiftvar));
  Multiplexer #(.width(32), .enable("false")) multiplexer_6 (
    .in0(out_9), .in1(imm_32), .out(multiplexer_6_out), .sel(ALUSrc));
  ALU alu_1 (
    .in1(RD1), .in2(multiplexer_6_out), .result(out_8), .ALUOp(ALUOp), .juedge_overflow(judge),
    .overflow(overflow), .equal(equal_sign), .in_1(multiplexer_5_out));
  DM dm_1 (
    .Address(out_8), .DataWrite(out_9), .MemWrite(out_7), .MemRead(MemRead), .rst(rst), .clk(clk),
    .out_10(ReadData), .b_or_h(b_or_h), .signExt(signExt), .not_word(not_word));
  sel_B sel_b_1 (.branch(branch), .equal(equal_sign), .in_3(RD1), .judge(rt), .branchOp(branchOp), .result(if_branch));

  // Other names for the same wires on the sheet: MemAddr[31:0] = out_8; MemWrite = out_7; operation[31:0] = out_2;
  //   pc[31:0] = out_3; RD2[31:0] = out_9; RegAddr[4:0] = out_5; RegData[31:0] = out_6; RegWrite = out_4

  // Notes on the sheet:
  //   $ra
  //   jal ?
  //   16-20
endmodule

module IFU (
  input  [31:0] npc,
  input  in_2,
  input  in_3,
  output [31:0] pc,
  output [31:0] \output 
);

  wire comparator_1_eq;
  wire [11:0] bit_extender_1_out;
  wire [31:0] PC_q, shifter_1_out, subtractor_1_out;

  Register #(.width(32)) u_PC (.D(npc), .Q(PC_q), .clk(in_2), .clr(in_3));  // open: en
  Comparator #(.width(32), .mode("unsigned")) comparator_1 (
    .a(PC_q), .b({32{1'b0}}), .eq(comparator_1_eq));  // open: gt, lt
  Multiplexer #(.width(32), .enable("false")) multiplexer_1 (
    .in0(PC_q), .in1(32'h3000), .out(pc), .sel(comparator_1_eq));
  Subtractor #(.width(32)) subtractor_1 (.a(pc), .b(32'h3000), .out(subtractor_1_out));  // open: bin, bout
  Shifter #(.width(32), .shift("lr")) shifter_1 (.in(subtractor_1_out), .\dist (5'b00010), .out(shifter_1_out));
  Bit_Extender #(.in_width(32), .out_width(12)) bit_extender_1 (.in(shifter_1_out), .out(bit_extender_1_out));
  ROM #(.addrWidth(12), .dataWidth(32)) rom_1 (.addr(bit_extender_1_out), .data(\output ));  // open: sel

  // Other names for the same wires on the sheet: clk = in_2; rst = in_3

  // Notes on the sheet:
  //   contents of rom_1 (hex, n*v repeats v):
  //   24100000 2411fc18 241203e8 3c138000 3c148000 36940001 3c157fff 36b5ffff 3c167fff 36d6fffe 12100015
  //   12b60016 16110017 16730018 1a000019 1ac0001a 1e40001b 1e20001c c000c30 c000c32 34023274 401809
  //   34023294 401809 ae080000 ae090000 ae0a0000 ae0b0000 ae0c0000 ae0d0000 2402000a c 21080001 8000c0b
  //   21080001 8000c0c 21290001 8000c0d 21290001 8000c0e 214a0001 8000c0f 214a0001 8000c10 216b0001
  //   8000c11 216b0001 8000c12 208c0001 3e00008 208c0001 3e00008 21ad0001 600008 21ad0001 600008
endmodule

module NPC (
  input  [31:0] pc,
  input  jump,
  input  branch,
  input  [31:0] offset,
  input  [25:0] J_address,
  input  [31:0] reg_address,
  input  jr,
  output [31:0] pc_4,
  output [31:0] npc
);

  wire [31:0] adder_2_out, multiplexer_1_out, multiplexer_2_out, shifter_1_out;

  Shifter #(.width(32)) shifter_1 (.in(offset), .\dist (5'b00010), .out(shifter_1_out));
  Adder #(.width(32)) adder_1 (.a(pc), .b(32'h4), .out(pc_4));  // open: cin, cout
  Adder #(.width(32)) adder_2 (.a(pc_4), .b(shifter_1_out), .out(adder_2_out));  // open: cin, cout
  Multiplexer #(.width(32), .enable("false")) multiplexer_1 (
    .in0(pc_4), .in1(adder_2_out), .out(multiplexer_1_out), .sel(branch));
  Multiplexer #(.width(32), .enable("false")) multiplexer_2 (
    .in0({pc_4[31:28], J_address, 2'b00}), .in1(reg_address), .out(multiplexer_2_out), .sel(jr));
  Multiplexer #(.width(32), .enable("false")) multiplexer_3 (
    .in0(multiplexer_1_out), .in1(multiplexer_2_out), .out(npc), .sel(jump));
endmodule

module GRF (
  input  reset,
  input  clk,
  input  WE,
  input  [4:0] A1,
  input  [4:0] A2,
  input  [4:0] A3,
  input  [31:0] \input ,
  output [31:0] RD1,
  output [31:0] RD2
);

  wire [31:0] _0, _1, _2, _3, _4, _5, _6, _7, _8, _9, _10, _11, _12, _13, _14, _15, _16, _17, _18, _19, _20,
       _21, _22, _23, _24, _25, _26, _27, _28, _29, _30, _31, O0, O1, O2, O3, O4, O5, O6, O7, O8, O9, O10,
       O11, O12, O13, O14, O15, O16, O17, O18, O19, O20, O21, O22, O23, O24, O25, O26, O27, O28, O29, O30,
       O31;

  Demultiplexer #(.select(5), .width(32), .tristate("true")) demultiplexer_1 (
    .out0(_0), .out1(_1), .out2(_2), .out3(_3), .out4(_4), .out5(_5), .out6(_6), .out7(_7), .out8(_8),
    .out9(_9), .out10(_10), .out11(_11), .out12(_12), .out13(_13), .out14(_14), .out15(_15), .out16(_16),
    .out17(_17), .out18(_18), .out19(_19), .out20(_20), .out21(_21), .out22(_22), .out23(_23), .out24(_24),
    .out25(_25), .out26(_26), .out27(_27), .out28(_28), .out29(_29), .out30(_30), .out31(_31), .in(\input ),
    .sel(A3), .en(WE));
  Register #(.width(32)) register_1 (.D(_0), .en(1'b0), .Q(O0), .clk(clk), .clr(reset));
  Register #(.width(32)) register_2 (.D(_4), .en(WE), .Q(O4), .clk(clk), .clr(reset));
  Register #(.width(32)) register_3 (.D(_8), .en(WE), .Q(O8), .clk(clk), .clr(reset));
  Register #(.width(32)) register_4 (.D(_12), .en(WE), .Q(O12), .clk(clk), .clr(reset));
  Register #(.width(32)) register_5 (.D(_16), .en(WE), .Q(O16), .clk(clk), .clr(reset));
  Register #(.width(32)) register_6 (.D(_20), .en(WE), .Q(O20), .clk(clk), .clr(reset));
  Register #(.width(32)) register_7 (.D(_24), .en(WE), .Q(O24), .clk(clk), .clr(reset));
  Register #(.width(32)) register_8 (.D(_28), .en(WE), .Q(O28), .clk(clk), .clr(reset));
  Register #(.width(32)) register_9 (.D(_1), .en(WE), .Q(O1), .clk(clk), .clr(reset));
  Register #(.width(32)) register_10 (.D(_5), .en(WE), .Q(O5), .clk(clk), .clr(reset));
  Register #(.width(32)) register_11 (.D(_9), .en(WE), .Q(O9), .clk(clk), .clr(reset));
  Register #(.width(32)) register_12 (.D(_13), .en(WE), .Q(O13), .clk(clk), .clr(reset));
  Register #(.width(32)) register_13 (.D(_17), .en(WE), .Q(O17), .clk(clk), .clr(reset));
  Register #(.width(32)) register_14 (.D(_21), .en(WE), .Q(O21), .clk(clk), .clr(reset));
  Register #(.width(32)) register_15 (.D(_25), .en(WE), .Q(O25), .clk(clk), .clr(reset));
  Register #(.width(32)) register_16 (.D(_29), .en(WE), .Q(O29), .clk(clk), .clr(reset));
  Register #(.width(32)) register_17 (.D(_2), .en(WE), .Q(O2), .clk(clk), .clr(reset));
  Register #(.width(32)) register_18 (.D(_6), .en(WE), .Q(O6), .clk(clk), .clr(reset));
  Register #(.width(32)) register_19 (.D(_10), .en(WE), .Q(O10), .clk(clk), .clr(reset));
  Register #(.width(32)) register_20 (.D(_14), .en(WE), .Q(O14), .clk(clk), .clr(reset));
  Register #(.width(32)) register_21 (.D(_18), .en(WE), .Q(O18), .clk(clk), .clr(reset));
  Register #(.width(32)) register_22 (.D(_22), .en(WE), .Q(O22), .clk(clk), .clr(reset));
  Register #(.width(32)) register_23 (.D(_26), .en(WE), .Q(O26), .clk(clk), .clr(reset));
  Register #(.width(32)) register_24 (.D(_30), .en(WE), .Q(O30), .clk(clk), .clr(reset));
  Register #(.width(32)) register_25 (.D(_3), .en(WE), .Q(O3), .clk(clk), .clr(reset));
  Register #(.width(32)) register_26 (.D(_7), .en(WE), .Q(O7), .clk(clk), .clr(reset));
  Register #(.width(32)) register_27 (.D(_11), .en(WE), .Q(O11), .clk(clk), .clr(reset));
  Register #(.width(32)) register_28 (.D(_15), .en(WE), .Q(O15), .clk(clk), .clr(reset));
  Register #(.width(32)) register_29 (.D(_19), .en(WE), .Q(O19), .clk(clk), .clr(reset));
  Register #(.width(32)) register_30 (.D(_23), .en(WE), .Q(O23), .clk(clk), .clr(reset));
  Register #(.width(32)) register_31 (.D(_27), .en(WE), .Q(O27), .clk(clk), .clr(reset));
  Register #(.width(32)) register_32 (.D(_31), .en(WE), .Q(O31), .clk(clk), .clr(reset));
  Multiplexer #(.select(5), .width(32), .enable("false")) multiplexer_1 (
    .in0(O0), .in1(O1), .in2(O2), .in3(O3), .in4(O4), .in5(O5), .in6(O6), .in7(O7), .in8(O8), .in9(O9),
    .in10(O10), .in11(O11), .in12(O12), .in13(O13), .in14(O14), .in15(O15), .in16(O16), .in17(O17),
    .in18(O18), .in19(O19), .in20(O20), .in21(O21), .in22(O22), .in23(O23), .in24(O24), .in25(O25),
    .in26(O26), .in27(O27), .in28(O28), .in29(O29), .in30(O30), .in31(O31), .out(RD2), .sel(A2));
  Multiplexer #(.select(5), .width(32)) multiplexer_2 (
    .in0(O0), .in1(O1), .in2(O2), .in3(O3), .in4(O4), .in5(O5), .in6(O6), .in7(O7), .in8(O8), .in9(O9),
    .in10(O10), .in11(O11), .in12(O12), .in13(O13), .in14(O14), .in15(O15), .in16(O16), .in17(O17),
    .in18(O18), .in19(O19), .in20(O20), .in21(O21), .in22(O22), .in23(O23), .in24(O24), .in25(O25),
    .in26(O26), .in27(O27), .in28(O28), .in29(O29), .in30(O30), .in31(O31), .out(RD1), .sel(A1));  // open: en
endmodule

module ALU (
  input  [4:0] in_1,
  input  juedge_overflow,
  input  [3:0] ALUOp,
  input  [31:0] in1,
  input  [31:0] in2,
  output [31:0] result,
  output equal,
  output overflow
);

  wire add, comparator_1_lt, comparator_2_lt, or_2_out, sub;
  wire [31:0] addu, \and , Arth_right, logical_left, logical_right, lui, \nor , \or , sign_compare_slt, subu,
       unsigned_compare_sltu, \xor ;

  assign \and  = in1 & in2;  // AND_Gate and_1, 32 bits wide
  assign \or  = in1 | in2;  // OR_Gate or_1, 32 bits wide
  Adder #(.width(32)) adder_1 (.a(in1), .b(in2), .out(addu), .cout(add));  // open: cin
  Subtractor #(.width(32)) subtractor_1 (.a(in1), .b(in2), .out(subu), .bout(sub));  // open: bin
  Shifter #(.width(32)) shifter_1 (.in(in2), .\dist (5'b10000), .out(lui));
  assign \xor  = in1 ^ in2;  // XOR_Gate xor_1, 32 bits wide
  assign \nor  = ~(in1 | in2);  // NOR_Gate nor_1, 32 bits wide
  Shifter #(.width(32)) shifter_2 (.in(in2), .\dist (in_1), .out(logical_left));
  Shifter #(.width(32), .shift("lr")) shifter_3 (.in(in2), .\dist (in_1), .out(logical_right));
  Shifter #(.width(32), .shift("ar")) shifter_4 (.in(in2), .\dist (in_1), .out(Arth_right));
  Comparator #(.width(32)) comparator_1 (.a(in1), .b(in2), .lt(comparator_1_lt));  // open: gt, eq
  Comparator #(.width(32), .mode("unsigned")) comparator_2 (.a(in1), .b(in2), .lt(comparator_2_lt));  // open: gt, eq
  assign sign_compare_slt = {{31{1'b0}}, comparator_1_lt};  // Bit_Extender bit_extender_1
  assign unsigned_compare_sltu = {{31{1'b0}}, comparator_2_lt};  // Bit_Extender bit_extender_2
  Comparator #(.width(32), .mode("unsigned")) comparator_3 (.a(subu), .b({32{1'b0}}), .eq(equal));  // open: gt, lt
  or or_2 (or_2_out, add, sub);
  Multiplexer #(.select(4), .width(32), .enable("false")) multiplexer_1 (
    .in0(\and ), .in1(\or ), .in2(addu), .in3(subu), .in4(lui), .in5(\xor ), .in6(\nor ), .in7(logical_left),
    .in8(logical_right), .in9(Arth_right), .in10(sign_compare_slt), .in11(unsigned_compare_sltu),
    .out(result), .sel(ALUOp));  // open: in12, in13, in14, in15
  and and_2 (overflow, or_2_out, juedge_overflow);

  // Other names for the same wires on the sheet: judge_overflow = juedge_overflow; OP[3:0] = ALUOp; shift[4:0] = in_1

  // Notes on the sheet:
  //   lui-shift
endmodule

module Controller (
  input  [5:0] opcode,
  input  [5:0] funct,
  output out_3,
  output out_4,
  output out_5,
  output out_6,
  output out_7,
  output out_8,
  output out_9,
  output out_10,
  output out_11,
  output out_12,
  output out_13,
  output out_14,
  output out_15,
  output out_16,
  output out_17,
  output out_18,
  output out_19,
  output out_20,
  output [2:0] out_21,
  output [3:0] out_22
);

  wire add, addi, addiu, \and , andi, beq, bgez, bgtz, blez, bltz, bne, j, jal, jalr, jr, lb, lbu, lh, lhu,
       lui, lw, \nor , \or , ori, R_out, sb, sh, sll, sllv, slt, slti, sltiu, sltu, sra, srav, srl, srlv,
       sub, sw, syscall, \xor , xori;
  wire [15:0] not_5_out, not_12_out;

  or RegDst (out_9, sltu, slt, jalr, jr, srav, add, sub, \and , \or , \xor , \nor , sra, srlv, sllv, srl, sll);
  not not_1 (not_5_out[15], opcode[5]);
  not not_2 (not_5_out[9], opcode[3]);
  not not_3 (not_5_out[12], opcode[4]);
  not not_4 (not_5_out[6], opcode[2]);
  not not_5 (not_5_out[0], opcode[0]);
  not not_6 (not_5_out[3], opcode[1]);
  or ALUSrc (out_10, lb, lbu, lh, lhu, sb, sh, lw, sw, slti, ori, lui, sltiu, addi, addiu, andi, xori);
  and u_ori (ori, not_5_out[15], not_5_out[12], opcode[3], opcode[2], not_5_out[3], opcode[0]);
  and u_lw (lw, opcode[5], not_5_out[12], not_5_out[9], not_5_out[6], opcode[1], opcode[0]);
  and u_sw (sw, opcode[5], not_5_out[12], opcode[3], not_5_out[6], opcode[1], opcode[0]);
  and u_beq (beq, not_5_out[15], not_5_out[12], not_5_out[9], opcode[2], not_5_out[3], not_5_out[0]);
  and u_lui (lui, not_5_out[15], not_5_out[12], opcode[3], opcode[2], opcode[1], opcode[0]);
  and R (R_out, not_5_out[15], not_5_out[12], not_5_out[9], not_5_out[6], not_5_out[3], not_5_out[0]);
  and u_j (j, not_5_out[15], not_5_out[12], not_5_out[9], not_5_out[6], opcode[1], not_5_out[0]);
  and u_jal (jal, not_5_out[15], not_5_out[12], not_5_out[9], not_5_out[6], opcode[1], opcode[0]);
  and u_addi (addi, not_5_out[15], not_5_out[12], opcode[3], not_5_out[6], not_5_out[3], not_5_out[0]);
  and u_andi (andi, not_5_out[15], not_5_out[12], opcode[3], opcode[2], not_5_out[3], not_5_out[0]);
  and u_addiu (addiu, not_5_out[15], not_5_out[12], opcode[3], not_5_out[6], not_5_out[3], opcode[0]);
  and u_xori (xori, not_5_out[15], not_5_out[12], opcode[3], opcode[2], opcode[1], not_5_out[0]);
  and u_bne (bne, not_5_out[15], not_5_out[12], not_5_out[9], opcode[2], not_5_out[3], opcode[0]);
  and u_bgtz (bgtz, not_5_out[15], not_5_out[12], not_5_out[9], opcode[2], opcode[1], opcode[0]);
  and u_bgez (bgez, not_5_out[15], not_5_out[12], not_5_out[9], not_5_out[6], not_5_out[3], opcode[0]);
  and u_blez (blez, not_5_out[15], not_5_out[12], not_5_out[9], opcode[2], opcode[1], not_5_out[0]);
  and u_bltz (bltz, not_5_out[15], not_5_out[12], not_5_out[9], not_5_out[6], not_5_out[3], opcode[0]);
  and u_slti (slti, not_5_out[15], not_5_out[12], opcode[3], not_5_out[6], opcode[1], not_5_out[0]);
  and u_sltiu (sltiu, not_5_out[15], not_5_out[12], opcode[3], not_5_out[6], opcode[1], opcode[0]);
  and u_sb (sb, opcode[5], not_5_out[12], opcode[3], not_5_out[6], not_5_out[3], not_5_out[0]);
  and u_sh (sh, opcode[5], not_5_out[12], opcode[3], not_5_out[6], not_5_out[3], opcode[0]);
  and u_lhu (lhu, opcode[5], not_5_out[12], not_5_out[9], opcode[2], not_5_out[3], opcode[0]);
  and u_lbu (lbu, opcode[5], not_5_out[12], not_5_out[9], opcode[2], not_5_out[3], not_5_out[0]);
  and u_lh (lh, opcode[5], not_5_out[12], not_5_out[9], not_5_out[6], not_5_out[3], opcode[0]);
  and u_lb (lb, opcode[5], not_5_out[12], not_5_out[9], not_5_out[6], not_5_out[3], not_5_out[0]);
  or MemtoReg (out_11, lw, lb, lbu, lh, lhu);
  not not_7 (not_12_out[15], funct[5]);
  not not_8 (not_12_out[12], funct[4]);
  or RegWrite (out_12, lb, lbu, lh, lhu, jalr, jal, slti, sltiu, addi, addiu, slt, \xor , \and , add, sub, lw, ori, lui, \or , \nor , sltu, andi, xori, sll, srl, sllv, srlv, sra, srav);
  not not_9 (not_12_out[3], funct[1]);
  not not_10 (not_12_out[9], funct[3]);
  not not_11 (not_12_out[6], funct[2]);
  not not_12 (not_12_out[0], funct[0]);
  or MemRead (out_13, sh, lw, lb, lbu, lh, lhu, sb);
  and u_sllv (sllv, R_out, not_12_out[15], not_12_out[12], not_12_out[9], funct[2], not_12_out[3], not_12_out[0]);
  and u_add (add, R_out, funct[5], not_12_out[12], not_12_out[9], not_12_out[6], not_12_out[3], not_12_out[0]);
  and u_sub (sub, R_out, funct[5], not_12_out[12], not_12_out[9], not_12_out[6], funct[1], not_12_out[0]);
  and u_and (\and , R_out, funct[5], not_12_out[12], not_12_out[9], funct[2], not_12_out[3], not_12_out[0]);
  and u_or (\or , R_out, funct[5], not_12_out[12], not_12_out[9], funct[2], not_12_out[3], funct[0]);
  and u_xor (\xor , funct[5], not_12_out[12], not_12_out[9], funct[2], funct[1], not_12_out[0], R_out);
  and u_nor (\nor , R_out, funct[5], not_12_out[12], not_12_out[9], funct[2], funct[1], funct[0]);
  and u_slt (slt, R_out, funct[5], not_12_out[12], funct[3], not_12_out[6], funct[1], not_12_out[0]);
  and u_sltu (sltu, R_out, funct[5], not_12_out[12], funct[3], not_12_out[6], funct[1], funct[0]);
  and u_sll (sll, not_12_out[15], not_12_out[12], not_12_out[9], not_12_out[6], not_12_out[3], not_12_out[0], R_out);
  and u_srl (srl, R_out, not_12_out[15], not_12_out[12], not_12_out[9], not_12_out[6], funct[1], not_12_out[0]);
  and u_sra (sra, R_out, not_12_out[15], not_12_out[12], not_12_out[9], not_12_out[6], funct[1], funct[0]);
  and u_srlv (srlv, R_out, not_12_out[15], not_12_out[12], not_12_out[9], funct[2], funct[1], not_12_out[0]);
  and u_srav (srav, R_out, not_12_out[15], not_12_out[12], not_12_out[9], funct[2], funct[1], funct[0]);
  and u_jr (jr, R_out, not_12_out[15], not_12_out[12], funct[3], not_12_out[6], not_12_out[3], not_12_out[0]);
  and u_jalr (jalr, R_out, not_12_out[15], not_12_out[12], funct[3], not_12_out[6], not_12_out[3], funct[0]);
  and u_syscall (syscall, R_out, not_12_out[15], not_12_out[12], funct[3], funct[2], not_12_out[3], not_12_out[0]);
  or MemWrite (out_14, sw, sb, sh);
  or branch (out_3, beq, bne, bgez, bgtz, blez, bltz);
  or ALUOp3 (out_22[3], srav, slt, sltu, slti, sltiu, srl, srlv, sra);
  or ALUOp2 (out_22[2], sll, \nor , beq, lui, \xor , xori, sllv);
  or ALUOp1 (out_22[1], lb, lbu, lh, lhu, sb, sh, sltu, \nor , add, sub, slt, lw, sw, beq, addi, addiu, slti, sll, sllv);
  or ALUOp0 (out_22[0], srav, sll, sltiu, sltu, \xor , sub, \or , ori, xori, sllv, sra);
  or EXTOp (out_4, bltz, blez, bgtz, addi, addiu, slti, sltiu, sh, beq, sw, lw, lb, lbu, lh, lhu, sb, bgez, bne);
  buf flowjudge (out_5, addi);  // OR_Gate
  buf syscall_2 (out_6, syscall);  // OR_Gate
  or not_word (out_7, lb, lbu, lh, lhu, sb, sh);
  or b_or_h (out_8, lh, lhu, sh);
  or b_h_signExt (out_15, lb, lh);
  or jump (out_16, jalr, jr, jal, j);
  or JR_2 (out_17, jalr, jr);
  or shiftvar (out_18, srlv, srav, sllv);
  buf ralink (out_19, jal);  // OR_Gate
  or PC_4 (out_20, jal, jalr);
  buf bOp2 (out_21[2], bne);  // OR_Gate
  or bOp1 (out_21[1], blez, bgtz);
  or bOp0 (out_21[0], bltz, bgez, blez);
endmodule

module EXT (
  input  [15:0] in_1,
  input  EXTOp,
  output [31:0] out_3
);

  wire [31:0] bit_extender_1_out, bit_extender_2_out;

  assign bit_extender_1_out = {{16{1'b0}}, in_1};  // Bit_Extender bit_extender_1
  assign bit_extender_2_out = {{16{in_1[15]}}, in_1};  // Bit_Extender bit_extender_2
  Multiplexer #(.width(32), .enable("false")) multiplexer_1 (
    .in0(bit_extender_1_out), .in1(bit_extender_2_out), .out(out_3), .sel(EXTOp));
endmodule

module DM (
  input  not_word,
  input  b_or_h,
  input  signExt,
  input  [31:0] Address,
  input  [31:0] DataWrite,
  input  clk,
  input  rst,
  input  MemWrite,
  input  MemRead,
  output [31:0] out_10
);

  wire [11:0] bit_extender_1_out;
  wire [31:0] dataread, horb_1_load, multiplexer_1_out, save_data, shifter_1_out;

  Shifter #(.width(32), .shift("lr")) shifter_1 (.in(Address), .\dist (5'b00010), .out(shifter_1_out));
  Bit_Extender #(.in_width(32), .out_width(12)) bit_extender_1 (.in(shifter_1_out), .out(bit_extender_1_out));
  Multiplexer #(.width(32), .enable("false")) multiplexer_1 (
    .in0(DataWrite), .in1(save_data), .out(multiplexer_1_out), .sel(not_word));
  HorB horb_1 (
    .signExt(signExt), .b_or_h(b_or_h), .write(DataWrite), .read(dataread), .address(Address),
    .load(horb_1_load), .save(save_data));
  RAM #(.addrWidth(12), .dataWidth(32), .bus("separate")) ram_1 (
    .addr(bit_extender_1_out), .din(multiplexer_1_out), .data(dataread), .str(MemWrite), .clk(clk),
    .ld(MemRead), .clr(rst));  // open: sel
  Multiplexer #(.width(32), .enable("false")) multiplexer_2 (
    .in0(dataread), .in1(horb_1_load), .out(out_10), .sel(not_word));

  // Notes on the sheet:
  //   when we need to save/load byte/half  memread must be 1
endmodule

module InstructionSplitter (
  input  [31:0] in_1,
  output [5:0] opcode,
  output [4:0] rs,
  output [4:0] rt,
  output [4:0] rd,
  output [4:0] shamt,
  output [5:0] funct,
  output [15:0] imm,
  output [25:0] address
);


  assign address = in_1[25:0];
  assign funct = in_1[5:0];
  assign imm = in_1[15:0];
  assign opcode = in_1[31:26];
  assign rd = in_1[15:11];
  assign rs = in_1[25:21];
  assign rt = in_1[20:16];
  assign shamt = in_1[10:6];

  // Other names for the same wires on the sheet: _0 = in_1[0]; _1 = in_1[1]; _2 = in_1[2]; _3 = in_1[3]; _4 = in_1[4];
  //   _5 = in_1[5]; _6 = in_1[6]; _7 = in_1[7]; _8 = in_1[8]; _9 = in_1[9]; _10 = in_1[10]; _11 = in_1[11];
  //   _12 = in_1[12]; _13 = in_1[13]; _14 = in_1[14]; _15 = in_1[15]; _16 = in_1[16]; _17 = in_1[17]; _18 = in_1[18];
  //   _19 = in_1[19]; _20 = in_1[20]; _21 = in_1[21]; _22 = in_1[22]; _23 = in_1[23]; _24 = in_1[24]; _25 = in_1[25];
  //   _26 = in_1[26]; _27 = in_1[27]; _28 = in_1[28]; _29 = in_1[29]; _30 = in_1[30]; _31 = in_1[31]
endmodule

module HorB (
  input  signExt,
  input  b_or_h,
  input  [31:0] write,
  input  [31:0] read,
  input  [31:0] address,
  output [31:0] load,
  output [31:0] save
);

  wire b_0__or_h_1_t, first_byte, first_half, last_byte, second_byte, second_half, third_byte;
  wire [7:0] multiplexer_1_out, multiplexer_7_out, multiplexer_8_out, multiplexer_9_out, multiplexer_10_out;
  wire [15:0] multiplexer_2_out, multiplexer_5_out, multiplexer_6_out;
  wire [31:0] bit_extender_1_out, bit_extender_2_out, bit_extender_3_out, bit_extender_4_out,
       multiplexer_3_out, multiplexer_4_out;

  Multiplexer #(.select(2), .width(8), .enable("false")) multiplexer_1 (
    .in0(read[7:0]), .in1(read[15:8]), .in2(read[23:16]), .in3(read[31:24]), .out(multiplexer_1_out),
    .sel(address[1:0]));
  Multiplexer #(.width(16), .enable("false")) multiplexer_2 (
    .in0(read[15:0]), .in1(read[31:16]), .out(multiplexer_2_out), .sel(address[1]));
  Decoder #(.select(2), .enable("false")) decoder_1 (
    .out0(first_byte), .out1(second_byte), .out2(third_byte), .out3(last_byte), .sel(address[1:0]));
  Decoder #(.enable("false")) decoder_2 (.out0(first_half), .out1(second_half), .sel(address[1]));
  assign bit_extender_1_out = {{24{1'b0}}, multiplexer_1_out};  // Bit_Extender bit_extender_1
  assign bit_extender_2_out = {{24{multiplexer_1_out[7]}}, multiplexer_1_out};  // Bit_Extender bit_extender_2
  assign bit_extender_3_out = {{16{1'b0}}, multiplexer_2_out};  // Bit_Extender bit_extender_3
  assign bit_extender_4_out = {{16{multiplexer_2_out[15]}}, multiplexer_2_out};  // Bit_Extender bit_extender_4
  Multiplexer #(.width(32), .enable("false")) multiplexer_3 (
    .in0(bit_extender_1_out), .in1(bit_extender_2_out), .out(multiplexer_3_out), .sel(signExt));
  Multiplexer #(.width(32), .enable("false")) multiplexer_4 (
    .in0(bit_extender_3_out), .in1(bit_extender_4_out), .out(multiplexer_4_out), .sel(signExt));
  Multiplexer #(.width(16), .enable("false")) multiplexer_5 (
    .in0(read[15:0]), .in1(write[15:0]), .out(multiplexer_5_out), .sel(first_half));
  Multiplexer #(.width(16), .enable("false")) multiplexer_6 (
    .in0(read[31:16]), .in1(write[15:0]), .out(multiplexer_6_out), .sel(second_half));
  Multiplexer #(.width(8), .enable("false")) multiplexer_7 (
    .in0(read[7:0]), .in1(write[7:0]), .out(multiplexer_7_out), .sel(first_byte));
  Multiplexer #(.width(8), .enable("false")) multiplexer_8 (
    .in0(read[15:8]), .in1(write[7:0]), .out(multiplexer_8_out), .sel(second_byte));
  Multiplexer #(.width(8), .enable("false")) multiplexer_9 (
    .in0(read[23:16]), .in1(write[7:0]), .out(multiplexer_9_out), .sel(third_byte));
  Multiplexer #(.width(8), .enable("false")) multiplexer_10 (
    .in0(read[31:24]), .in1(write[7:0]), .out(multiplexer_10_out), .sel(last_byte));
  Multiplexer #(.width(32), .enable("false")) multiplexer_11 (
    .in0(multiplexer_3_out), .in1(multiplexer_4_out), .out(load), .sel(b_0__or_h_1_t));
  Multiplexer #(.width(32), .enable("false")) multiplexer_12 (
    .in0({multiplexer_10_out, multiplexer_9_out, multiplexer_8_out, multiplexer_7_out}),
    .in1({multiplexer_6_out, multiplexer_5_out}), .out(save), .sel(b_or_h));

  // Other names for the same wires on the sheet: b_0__or_h_1 = b_or_h; savebyte[7:0] = write[7:0];
  //   savehalf[15:0] = write[15:0]

  // Notes on the sheet:
  //   when save or load a word 1-0 is 00
  //   when save or load a half word judge 1 is 0 or 1
  //   when save or load a byte judge 1-0 
  //   memread=1
endmodule

module sel_B (
  input  branch,
  input  equal,
  input  [31:0] in_3,
  input  [4:0] judge,
  input  [2:0] branchOp,
  output result
);

  wire comparator_1_lt, comparator_2_eq, comparator_2_gt, comparator_3_gt, comparator_4_eq, comparator_4_lt,
       multiplexer_1_out, multiplexer_2_out, multiplexer_3_out, not_1_out, or_1_out, or_2_out;

  Multiplexer #(.enable("false")) multiplexer_1 (
    .in0(equal), .in1(not_1_out), .out(multiplexer_1_out), .sel(branchOp[2]));
  not not_1 (not_1_out, equal);
  Comparator #(.width(32)) comparator_1 (.a(in_3), .b({32{1'b0}}), .lt(comparator_1_lt));  // open: gt, eq
  Comparator #(.width(32)) comparator_2 (
    .a(in_3), .b({32{1'b0}}), .gt(comparator_2_gt), .eq(comparator_2_eq));  // open: lt
  Comparator #(.width(32)) comparator_3 (.a(in_3), .b({32{1'b0}}), .gt(comparator_3_gt));  // open: eq, lt
  Comparator #(.width(32)) comparator_4 (
    .a(in_3), .b({32{1'b0}}), .eq(comparator_4_eq), .lt(comparator_4_lt));  // open: gt
  or or_1 (or_1_out, comparator_4_eq, comparator_4_lt);
  or or_2 (or_2_out, comparator_2_gt, comparator_2_eq);
  Multiplexer #(.enable("false")) multiplexer_2 (
    .in0(comparator_1_lt), .in1(or_2_out), .out(multiplexer_2_out), .sel(judge[0]));
  Multiplexer #(.select(2), .enable("false")) multiplexer_3 (
    .in0(multiplexer_1_out), .in1(multiplexer_2_out), .in2(comparator_3_gt), .in3(or_1_out),
    .out(multiplexer_3_out), .sel(branchOp[1:0]));
  and and_1 (result, branch, multiplexer_3_out);

  // Other names for the same wires on the sheet: beq_bne = branchOp[2]

  // Notes on the sheet:
  //   select which kind of Branch-Op
endmodule
