// Logisim project fibonacci.circ as structural Verilog: 1 circuit, main circuit main
module main (
  input  [2:0] in_1,
  input  in_2,
  input  in_3,
  output [3:0] out_4
);

  wire counter_2_q, en;
  wire [2:0] counter_1_q;
  wire [3:0] adder_1_out, multiplexer_1_out, n_1_q, n_2_q;

  Counter #(.width(3), .max('h7), .ongoal("stay")) counter_1 (
    .Q(counter_1_q), .clk(in_2), .clr(in_3));  // open: load, D, count, carry
  Comparator #(.width(3), .mode("unsigned")) comparator_1 (.a(in_1), .b(counter_1_q), .gt(en));  // open: eq, lt
  Register #(.width(4)) n_1 (.D(adder_1_out), .en(en), .Q(n_1_q), .clk(in_2), .clr(in_3));
  Counter #(.width(1), .max('h1), .ongoal("stay")) counter_2 (
    .Q(counter_2_q), .clk(in_2), .clr(in_3));  // open: load, D, count, carry
  Multiplexer #(.width(4), .enable("false")) multiplexer_1 (
    .in0(4'b0001), .in1(n_1_q), .out(multiplexer_1_out), .sel(counter_2_q));
  Register #(.width(4)) n_2 (.D(multiplexer_1_out), .en(en), .Q(n_2_q), .clk(in_2), .clr(in_3));
  Adder #(.width(4)) adder_1 (.a(n_2_q), .b(n_1_q), .out(adder_1_out));  // open: cin, cout
  Multiplexer #(.width(4), .enable("false")) multiplexer_2 (.in0(adder_1_out), .in1(4'b0000), .out(out_4), .sel(en));

  // Other names for the same wires on the sheet: clk = in_2; rst = in_3
endmodule
