// Logisim project fibonacci_2.circ as structural Verilog: 8 circuits, main circuit main
module main (
  input  [31:0] \input ,
  output [31:0] \output 
);

  wire count_freeze, count_n_low;

  \計數邏輯  count (.\input (\input ), .in_2(1'b0), .n_low(count_n_low), .freeze(count_freeze));
  \計算邏輯  calculate (.in_1(count_n_low), .in_2(count_freeze), .in_3(1'b0), .out_4(\output ));
endmodule

module \矩陣乘法  (
  input  [31:0] in_1,
  input  [31:0] in_2,
  input  [31:0] in_3,
  input  [31:0] in_4,
  input  [31:0] in_5,
  input  [31:0] in_6,
  input  [31:0] in_7,
  input  [31:0] in_8,
  output [31:0] c11,
  output [31:0] c12,
  output [31:0] c21,
  output [31:0] c22
);

  wire [31:0] multiplier_1_out, multiplier_2_out, multiplier_3_out, multiplier_4_out, multiplier_5_out,
       multiplier_6_out, multiplier_7_out, multiplier_8_out;

  Multiplier #(.width(32)) multiplier_1 (.a(in_1), .b(in_5), .out(multiplier_1_out));  // open: cin, cout
  Multiplier #(.width(32)) multiplier_2 (.a(in_2), .b(in_7), .out(multiplier_2_out));  // open: cin, cout
  Multiplier #(.width(32)) multiplier_3 (.a(in_1), .b(in_6), .out(multiplier_3_out));  // open: cin, cout
  Multiplier #(.width(32)) multiplier_4 (.a(in_2), .b(in_8), .out(multiplier_4_out));  // open: cin, cout
  Multiplier #(.width(32)) multiplier_5 (.a(in_3), .b(in_5), .out(multiplier_5_out));  // open: cin, cout
  Multiplier #(.width(32)) multiplier_6 (.a(in_4), .b(in_7), .out(multiplier_6_out));  // open: cin, cout
  Multiplier #(.width(32)) multiplier_7 (.a(in_3), .b(in_6), .out(multiplier_7_out));  // open: cin, cout
  Multiplier #(.width(32)) multiplier_8 (.a(in_4), .b(in_8), .out(multiplier_8_out));  // open: cin, cout
  Adder #(.width(32)) adder_1 (.a(multiplier_1_out), .b(multiplier_2_out), .out(c11));  // open: cin, cout
  Adder #(.width(32)) adder_2 (.a(multiplier_3_out), .b(multiplier_4_out), .out(c12));  // open: cin, cout
  Adder #(.width(32)) adder_3 (.a(multiplier_5_out), .b(multiplier_6_out), .out(c21));  // open: cin, cout
  Adder #(.width(32)) adder_4 (.a(multiplier_7_out), .b(multiplier_8_out), .out(c22));  // open: cin, cout

  // Other names for the same wires on the sheet: a11[31:0] = in_1; a12[31:0] = in_2; a21[31:0] = in_3;
  //   a22[31:0] = in_4; b11[31:0] = in_5; b12[31:0] = in_6; b21[31:0] = in_7; b22[31:0] = in_8
endmodule

module \寄存器矩陣  (
  input  [31:0] in_1,
  input  [31:0] in_2,
  input  [31:0] in_3,
  input  [31:0] in_4,
  input  in_5,
  input  clk,
  input  in_7,
  output [31:0] out_8,
  output [31:0] out_9,
  output [31:0] out_10,
  output [31:0] out_11
);

  Register #(.width(32)) register_1 (.D(in_1), .en(in_5), .Q(out_8), .clk(clk), .clr(in_7));
  Register #(.width(32)) register_2 (.D(in_2), .en(in_5), .Q(out_9), .clk(clk), .clr(in_7));
  Register #(.width(32)) register_3 (.D(in_3), .en(in_5), .Q(out_10), .clk(clk), .clr(in_7));
  Register #(.width(32)) register_4 (.D(in_4), .en(in_5), .Q(out_11), .clk(clk), .clr(in_7));

  // Other names for the same wires on the sheet: clr = in_7; ena = in_5
endmodule

module \矩陣MUX  (
  input  [31:0] in_1,
  input  [31:0] in_2,
  input  [31:0] in_3,
  input  [31:0] in_4,
  input  [31:0] in_5,
  input  [31:0] in_6,
  input  [31:0] in_7,
  input  [31:0] in_8,
  input  in_9,
  output [31:0] _11,
  output [31:0] _12,
  output [31:0] _21,
  output [31:0] _22
);

  Multiplexer #(.width(32)) multiplexer_1 (.in0(in_1), .in1(in_5), .out(_11), .sel(in_9));  // open: en
  Multiplexer #(.width(32)) multiplexer_2 (.in0(in_2), .in1(in_6), .out(_12), .sel(in_9));  // open: en
  Multiplexer #(.width(32)) multiplexer_3 (.in0(in_3), .in1(in_7), .out(_21), .sel(in_9));  // open: en
  Multiplexer #(.width(32)) multiplexer_4 (.in0(in_4), .in1(in_8), .out(_22), .sel(in_9));  // open: en

  // Other names for the same wires on the sheet: a11[31:0] = in_1; a12[31:0] = in_2; a21[31:0] = in_3;
  //   a22[31:0] = in_4; b11[31:0] = in_5; b12[31:0] = in_6; b21[31:0] = in_7; b22[31:0] = in_8; select = in_9
endmodule

module \矩陣初始值  (
  output [31:0] _11,
  output [31:0] _12,
  output [31:0] _21,
  output [31:0] _22
);


  assign _11 = 32'h1;
  assign _12 = 32'h1;
  assign _21 = 32'h1;
  assign _22 = {32{1'b0}};
endmodule

module \單位陣  (
  output [31:0] _11,
  output [31:0] _12,
  output [31:0] _21,
  output [31:0] _22
);


  assign _11 = 32'h1;
  assign _12 = {32{1'b0}};
  assign _21 = {32{1'b0}};
  assign _22 = 32'h1;
endmodule

module \計算邏輯  (
  input  in_1,
  input  in_2,
  input  in_3,
  output [31:0] out_4
);

  wire clk, ena, init;
  wire [31:0] a11, a12, a21, a22, s11, s12, s21, s22, \乘方初值__11 , \乘方初值__12 , \乘方初值__21 , \乘方初值__22 ,
       \單位陣_2__11 , \單位陣_2__12 , \單位陣_2__21 , \單位陣_2__22 , \單位陣__11 , \單位陣__12 , \單位陣__21 , \單位陣__22 ,
       \矩陣乘法_1_c11 , \矩陣乘法_1_c12 , \矩陣乘法_1_c21 , \矩陣乘法_1_c22 , \進行平方運算_c11 , \進行平方運算_c12 , \進行平方運算_c21 ,
       \進行平方運算_c22 , \選擇器_2__11 , \選擇器_2__12 , \選擇器_2__21 , \選擇器_2__22 , \選擇器_3__11 , \選擇器_3__12 ,
       \選擇器_3__21 , \選擇器_3__22 , \選擇器__11 , \選擇器__12 , \選擇器__21 , \選擇器__22 ;

  Counter #(.width(1), .max('h1), .ongoal("stay")) counter_1 (
    .Q(init), .clk(clk), .clr(in_3));  // open: load, D, count, carry
  Clock clock_1 (.out(clk));
  not not_1 (ena, in_2);
  \單位陣  \u_單位陣  (._11(\單位陣__11 ), ._12(\單位陣__12 ), ._21(\單位陣__21 ), ._22(\單位陣__22 ));
  \矩陣MUX  \u_選擇器  (
    .in_1(\單位陣__11 ), .in_2(\單位陣__12 ), .in_3(\單位陣__21 ), .in_4(\單位陣__22 ), .in_5(a11), .in_6(a12),
    .in_7(a21), .in_8(a22), .in_9(in_1), ._11(\選擇器__11 ), ._12(\選擇器__12 ), ._21(\選擇器__21 ), ._22(\選擇器__22 ));
  \矩陣乘法  \u_進行平方運算  (
    .in_1(a11), .in_2(a12), .in_3(a21), .in_4(a22), .in_5(a11), .in_6(a12), .in_7(a21), .in_8(a22),
    .c11(\進行平方運算_c11 ), .c12(\進行平方運算_c12 ), .c21(\進行平方運算_c21 ), .c22(\進行平方運算_c22 ));
  \矩陣初始值  \u_乘方初值  (._11(\乘方初值__11 ), ._12(\乘方初值__12 ), ._21(\乘方初值__21 ), ._22(\乘方初值__22 ));
  \矩陣MUX  \u_選擇器_2  (
    .in_1(\乘方初值__11 ), .in_2(\乘方初值__12 ), .in_3(\乘方初值__21 ), .in_4(\乘方初值__22 ), .in_5(\進行平方運算_c11 ),
    .in_6(\進行平方運算_c12 ), .in_7(\進行平方運算_c21 ), .in_8(\進行平方運算_c22 ), .in_9(init), ._11(\選擇器_2__11 ),
    ._12(\選擇器_2__12 ), ._21(\選擇器_2__21 ), ._22(\選擇器_2__22 ));
  \單位陣  \u_單位陣_2  (._11(\單位陣_2__11 ), ._12(\單位陣_2__12 ), ._21(\單位陣_2__21 ), ._22(\單位陣_2__22 ));
  \矩陣乘法  \u_矩陣乘法_1  (
    .in_1(s11), .in_2(s12), .in_3(s21), .in_4(s22), .in_5(\選擇器__11 ), .in_6(\選擇器__12 ), .in_7(\選擇器__21 ),
    .in_8(\選擇器__22 ), .c11(\矩陣乘法_1_c11 ), .c12(\矩陣乘法_1_c12 ), .c21(\矩陣乘法_1_c21 ), .c22(\矩陣乘法_1_c22 ));
  \寄存器矩陣  \u_矩陣A  (
    .in_1(\選擇器_2__11 ), .in_2(\選擇器_2__12 ), .in_3(\選擇器_2__21 ), .in_4(\選擇器_2__22 ), .in_5(ena), .clk(clk),
    .in_7(in_3), .out_8(a11), .out_9(a12), .out_10(a21), .out_11(a22));
  \寄存器矩陣  \u_矩陣A_2  (
    .in_1(\選擇器_3__11 ), .in_2(\選擇器_3__12 ), .in_3(\選擇器_3__21 ), .in_4(\選擇器_3__22 ), .in_5(ena), .clk(clk),
    .in_7(in_3), .out_8(s11), .out_9(s12), .out_10(s21), .out_11(s22));
  \矩陣MUX  \u_選擇器_3  (
    .in_1(\單位陣_2__11 ), .in_2(\單位陣_2__12 ), .in_3(\單位陣_2__21 ), .in_4(\單位陣_2__22 ), .in_5(\矩陣乘法_1_c11 ),
    .in_6(\矩陣乘法_1_c12 ), .in_7(\矩陣乘法_1_c21 ), .in_8(\矩陣乘法_1_c22 ), .in_9(init), ._11(\選擇器_3__11 ),
    ._12(\選擇器_3__12 ), ._21(\選擇器_3__21 ), ._22(\選擇器_3__22 ));
  Multiplexer #(.width(32)) multiplexer_1 (.in0({32{1'b0}}), .in1(s12), .out(out_4), .sel(in_2));  // open: en

  // Other names for the same wires on the sheet: clr = in_3; freeze = in_2; n_low = in_1
endmodule

module \計數邏輯  (
  input  [31:0] \input ,
  input  in_2,
  output n_low,
  output freeze
);

  wire CLK, comparator_1_eq, init;
  wire [31:0] multiplexer_1_out, n, shifter_1_out;

  Counter #(.width(1), .max('h1), .ongoal("stay")) counter_1 (
    .Q(init), .clk(CLK), .clr(in_2));  // open: load, D, count, carry
  Clock clock_1 (.out(CLK));
  Shifter #(.width(32), .shift("lr")) shifter_1 (.in(n), .\dist (5'b00001), .out(shifter_1_out));
  Comparator #(.width(32), .mode("unsigned")) comparator_1 (
    .a(n), .b({32{1'b0}}), .eq(comparator_1_eq));  // open: gt, lt
  Multiplexer #(.width(32)) multiplexer_1 (
    .in0(\input ), .in1(shifter_1_out), .out(multiplexer_1_out), .sel(init));  // open: en
  Bit_Extender #(.in_width(32), .out_width(1)) bit_extender_1 (.in(n), .out(n_low));
  Multiplexer multiplexer_2 (.in0(1'b0), .in1(comparator_1_eq), .out(freeze), .sel(init));  // open: en
  Register #(.width(32)) register_1 (.D(multiplexer_1_out), .Q(n), .clk(CLK), .clr(in_2));  // open: en

  // Other names for the same wires on the sheet: clr = in_2
endmodule
