// Logisim project russia.circ as structural Verilog: 1 circuit, main circuit main
module main (
  input  [7:0] \input ,
  input  clk,
  input  reset,
  output [1:0] ouput
);

  wire and_2_out, or_2_out;
  wire [1:0] multiplexer_3_out;
  wire [7:0] and_1_out, multiplexer_1_out, multiplexer_2_out, or_1_out, register_1_q;

  assign and_1_out = \input  & register_1_q;  // AND_Gate and_1, 8 bits wide
  assign or_1_out = register_1_q | \input ;  // OR_Gate or_1, 8 bits wide
  or or_2 (or_2_out, and_1_out[0], and_1_out[1], and_1_out[2], and_1_out[3], and_1_out[4], and_1_out[5], and_1_out[6], and_1_out[7]);
  and and_2 (and_2_out, or_1_out[0], or_1_out[1], or_1_out[2], or_1_out[3], or_1_out[4], or_1_out[5], or_1_out[6], or_1_out[7]);
  Multiplexer #(.width(8), .enable("false")) multiplexer_1 (
    .in0(or_1_out), .in1({8{1'b0}}), .out(multiplexer_1_out), .sel(and_2_out));
  Multiplexer #(.width(8), .enable("false")) multiplexer_2 (
    .in0(multiplexer_1_out), .in1(and_1_out), .out(multiplexer_2_out), .sel(or_2_out));
  Register register_1 (.D(multiplexer_2_out), .Q(register_1_q), .clk(clk), .clr(reset));  // open: en
  Multiplexer #(.width(2), .enable("false")) multiplexer_3 (
    .in0(2'b10), .in1(2'b11), .out(multiplexer_3_out), .sel(and_2_out));
  Multiplexer #(.width(2), .enable("false")) multiplexer_4 (
    .in0(multiplexer_3_out), .in1(2'b01), .out(ouput), .sel(or_2_out));
endmodule
