// Logisim project voter_plus.circ as structural Verilog: 1 circuit, main circuit main
module main (
  input  [31:0] np,
  input  [7:0] vip,
  input  vvip,
  input  clk,
  input  rst,
  output [7:0] out_6
);

  wire or_3_out, voted_vvip_q;
  wire [3:0] bitadder_2_out, multiplier_1_out;
  wire [5:0] bitadder_1_out;
  wire [7:0] adder_1_out, adder_2_out, bit_extender_1_out, bit_extender_2_out, multiplexer_1_out, or_1_out,
       voted_vip_q;
  wire [31:0] or_2_out, voted_np_q;

  Register #(.width(32)) voted_np (.D(or_2_out), .Q(voted_np_q), .clk(clk), .clr(rst));  // open: en
  Register voted_vip (.D(or_1_out), .Q(voted_vip_q), .clk(clk), .clr(rst));  // open: en
  Register #(.width(1)) voted_vvip (.D(or_3_out), .Q(voted_vvip_q), .clk(clk), .clr(rst));  // open: en
  assign or_1_out = voted_vip_q | vip;  // OR_Gate or_1, 8 bits wide
  assign or_2_out = voted_np_q | np;  // OR_Gate or_2, 32 bits wide
  or or_3 (or_3_out, voted_vvip_q, vvip);
  BitAdder #(.width(32)) bitadder_1 (.in0(or_2_out), .out(bitadder_1_out));
  BitAdder bitadder_2 (.in0(or_1_out), .out(bitadder_2_out));
  Multiplier #(.width(4)) multiplier_1 (.a(bitadder_2_out), .b(4'b0100), .out(multiplier_1_out));  // open: cin, cout
  assign bit_extender_1_out = {{2{1'b0}}, bitadder_1_out};  // Bit_Extender bit_extender_1
  assign bit_extender_2_out = {{4{1'b0}}, multiplier_1_out};  // Bit_Extender bit_extender_2
  Multiplexer #(.width(8), .enable("false")) multiplexer_1 (
    .in0({8{1'b0}}), .in1(8'h10), .out(multiplexer_1_out), .sel(or_3_out));
  Adder adder_1 (.a(bit_extender_1_out), .b(bit_extender_2_out), .out(adder_1_out));  // open: cin, cout
  Adder adder_2 (.a(adder_1_out), .b(multiplexer_1_out), .out(adder_2_out));  // open: cin, cout
  Multiplexer #(.width(8), .enable("false")) multiplexer_2 (.in0(adder_2_out), .in1({8{1'b0}}), .out(out_6), .sel(rst));
endmodule
