// Logisim project ftoi.circ as structural Verilog: 1 circuit, main circuit ftoi
module ftoi (
  input  [15:0] float,
  output [31:0] \int 
);

  wire a, and_1_out, comparator_1_gt, \or , or_2_out;
  wire [4:0] subtractor_1_out, subtractor_2_out;
  wire [30:0] bit_extender_2_out, not_1_out;
  wire [31:0] adder_1_out, bit_extender_1_out, multiplexer_1_out, multiplexer_3_out, or_3_out, shifter_1_out,
       shifter_2_out, shifter_3_out;

  or or_1 (a, \or , or_2_out);
  assign {bit_extender_1_out[31:11], \or , bit_extender_1_out[9:0]} = {{22{1'b0}}, float[9:0]};  // Bit_Extender bit_extender_1
  // Probe on float[14:10]
  and and_1 (and_1_out, float[10], float[11], float[12], float[13], float[14]);
  or or_2 (or_2_out, float[10], float[11], float[12], float[13], float[14]);
  Comparator #(.width(5), .mode("unsigned")) comparator_1 (
    .a(float[14:10]), .b(5'b01111), .gt(comparator_1_gt));  // open: eq, lt
  // Probe on 5'b01111
  Subtractor #(.width(5)) subtractor_1 (.a(5'b01111), .b(float[14:10]), .out(subtractor_1_out));  // open: bin, bout
  // Probe on subtractor_1_out
  Subtractor #(.width(5)) subtractor_2 (.a(float[14:10]), .b(5'b01111), .out(subtractor_2_out));  // open: bin, bout
  Shifter #(.width(32), .shift("lr")) shifter_1 (
    .in({bit_extender_1_out[31:11], a, bit_extender_1_out[9:0]}), .\dist (subtractor_1_out),
    .out(shifter_1_out));
  Shifter #(.width(32)) shifter_2 (
    .in({bit_extender_1_out[31:11], a, bit_extender_1_out[9:0]}), .\dist (subtractor_2_out),
    .out(shifter_2_out));
  Multiplexer #(.width(32), .enable("false")) multiplexer_1 (
    .in0(shifter_1_out), .in1(shifter_2_out), .out(multiplexer_1_out), .sel(comparator_1_gt));
  Multiplexer #(.width(32), .enable("false")) multiplexer_2 (
    .in0(multiplexer_3_out), .in1({32{1'b0}}), .out(\int ), .sel(and_1_out));
  Shifter #(.width(32), .shift("lr")) shifter_3 (.in(multiplexer_1_out), .\dist (5'b01010), .out(shifter_3_out));
  Bit_Extender #(.in_width(32), .out_width(31)) bit_extender_2 (.in(shifter_3_out), .out(bit_extender_2_out));
  not not_1 (not_1_out[0], bit_extender_2_out[0]);
  not not_2 (not_1_out[1], bit_extender_2_out[1]);
  not not_3 (not_1_out[2], bit_extender_2_out[2]);
  not not_4 (not_1_out[3], bit_extender_2_out[3]);
  not not_5 (not_1_out[4], bit_extender_2_out[4]);
  not not_6 (not_1_out[5], bit_extender_2_out[5]);
  not not_7 (not_1_out[6], bit_extender_2_out[6]);
  not not_8 (not_1_out[7], bit_extender_2_out[7]);
  not not_9 (not_1_out[8], bit_extender_2_out[8]);
  not not_10 (not_1_out[9], bit_extender_2_out[9]);
  not not_11 (not_1_out[10], bit_extender_2_out[10]);
  not not_12 (not_1_out[11], bit_extender_2_out[11]);
  not not_13 (not_1_out[12], bit_extender_2_out[12]);
  not not_14 (not_1_out[13], bit_extender_2_out[13]);
  not not_15 (not_1_out[14], bit_extender_2_out[14]);
  not not_16 (not_1_out[15], bit_extender_2_out[15]);
  not not_17 (not_1_out[16], bit_extender_2_out[16]);
  not not_18 (not_1_out[17], bit_extender_2_out[17]);
  not not_19 (not_1_out[18], bit_extender_2_out[18]);
  not not_20 (not_1_out[19], bit_extender_2_out[19]);
  not not_21 (not_1_out[20], bit_extender_2_out[20]);
  not not_22 (not_1_out[21], bit_extender_2_out[21]);
  not not_23 (not_1_out[22], bit_extender_2_out[22]);
  not not_24 (not_1_out[23], bit_extender_2_out[23]);
  not not_25 (not_1_out[24], bit_extender_2_out[24]);
  not not_26 (not_1_out[25], bit_extender_2_out[25]);
  not not_27 (not_1_out[26], bit_extender_2_out[26]);
  not not_28 (not_1_out[27], bit_extender_2_out[27]);
  not not_29 (not_1_out[28], bit_extender_2_out[28]);
  not not_30 (not_1_out[29], bit_extender_2_out[29]);
  not not_31 (not_1_out[30], bit_extender_2_out[30]);
  Adder #(.width(32)) adder_1 (.a({1'b0, not_1_out}), .b(32'h1), .out(adder_1_out));  // open: cin, cout
  assign or_3_out = adder_1_out | 32'h80000000;  // OR_Gate or_3, 32 bits wide
  Multiplexer #(.width(32), .enable("false")) multiplexer_3 (
    .in0(shifter_3_out), .in1(or_3_out), .out(multiplexer_3_out), .sel(float[15]));

  // Other names for the same wires on the sheet: sign = float[15]
endmodule
