// Logisim project navigation_2020.circ as structural Verilog: 3 circuits, main circuit navigation
module navigation (
  input  [1:0] dir,
  input  clk,
  input  reset,
  output arrive,
  output hit
);

  wire [3:0] register_1_q, status_out_3;

  status status (.status(register_1_q), .dir(dir), .out_3(status_out_3));
  Register #(.width(4)) register_1 (.D(status_out_3), .Q(register_1_q), .clk(clk), .clr(reset));  // open: en
  \output  \output  (.in_1(register_1_q), .o(arrive), .hit(hit));
endmodule

module status (
  input  [3:0] status,
  input  [1:0] dir,
  output [3:0] out_3
);

  wire and_1_out, and_2_out, and_3_out, and_4_out, and_5_out, and_6_out, and_7_out, and_8_out, and_9_out,
       and_10_out, and_11_out, and_12_out, and_13_out, and_14_out, and_15_out, and_16_out, not_1_out,
       not_2_out, not_3_out, not_4_out, not_5_out, not_6_out, not_7_out, not_8_out, not_9_out, not_10_out,
       not_11_out, not_12_out, not_13_out, not_14_out, not_15_out, not_16_out, not_17_out, not_18_out,
       not_19_out, not_20_out, not_21_out, not_22_out, not_23_out, not_24_out, not_25_out, not_26_out,
       not_27_out, not_28_out;
  wire [2:0] bit_extender_1_out;

  Bit_Extender #(.in_width(4), .out_width(3)) bit_extender_1 (.in(status), .out(bit_extender_1_out));
  not not_1 (not_1_out, bit_extender_1_out[0]);
  not not_2 (not_2_out, dir[1]);
  not not_3 (not_3_out, dir[0]);
  not not_4 (not_4_out, dir[1]);
  not not_5 (not_5_out, bit_extender_1_out[1]);
  not not_6 (not_6_out, dir[1]);
  not not_7 (not_7_out, dir[1]);
  not not_8 (not_8_out, dir[0]);
  not not_9 (not_9_out, bit_extender_1_out[0]);
  not not_10 (not_10_out, dir[1]);
  not not_11 (not_11_out, bit_extender_1_out[0]);
  not not_12 (not_12_out, dir[0]);
  not not_13 (not_13_out, bit_extender_1_out[2]);
  not not_14 (not_14_out, bit_extender_1_out[1]);
  not not_15 (not_15_out, dir[1]);
  not not_16 (not_16_out, dir[0]);
  not not_17 (not_17_out, dir[0]);
  not not_18 (not_18_out, bit_extender_1_out[2]);
  not not_19 (not_19_out, bit_extender_1_out[0]);
  not not_20 (not_20_out, dir[1]);
  not not_21 (not_21_out, bit_extender_1_out[2]);
  not not_22 (not_22_out, bit_extender_1_out[1]);
  not not_23 (not_23_out, bit_extender_1_out[0]);
  not not_24 (not_24_out, bit_extender_1_out[2]);
  not not_25 (not_25_out, bit_extender_1_out[0]);
  not not_26 (not_26_out, dir[0]);
  not not_27 (not_27_out, dir[1]);
  not not_28 (not_28_out, dir[0]);
  and and_1 (and_1_out, bit_extender_1_out[1], not_1_out, not_2_out, not_3_out);
  or or_1 (out_3[2], and_1_out, and_2_out);
  and and_2 (and_2_out, bit_extender_1_out[1], bit_extender_1_out[0], not_4_out, dir[0]);
  and and_3 (and_3_out, not_5_out, bit_extender_1_out[0], not_6_out);
  and and_4 (and_4_out, bit_extender_1_out[0], not_7_out, not_8_out);
  and and_5 (and_5_out, bit_extender_1_out[1], not_9_out, not_10_out, dir[0]);
  and and_6 (and_6_out, bit_extender_1_out[1], not_11_out, dir[1], not_12_out);
  and and_7 (and_7_out, bit_extender_1_out[1], bit_extender_1_out[0], dir[1], dir[0]);
  and and_8 (and_8_out, not_13_out, not_14_out, not_15_out, not_16_out);
  and and_9 (and_9_out, bit_extender_1_out[0], dir[1], dir[0]);
  and and_10 (and_10_out, bit_extender_1_out[1], dir[1], dir[0]);
  and and_11 (and_11_out, bit_extender_1_out[1], bit_extender_1_out[0], not_17_out);
  and and_12 (and_12_out, not_18_out, not_19_out, not_20_out, dir[0]);
  and and_13 (and_13_out, not_21_out, not_22_out, not_23_out, dir[1]);
  and and_14 (and_14_out, not_24_out, not_25_out, dir[1], not_26_out);
  and and_15 (and_15_out, bit_extender_1_out[0], dir[1], dir[0]);
  and and_16 (and_16_out, bit_extender_1_out[1], bit_extender_1_out[0], not_27_out, not_28_out);
  or or_2 (out_3[1], and_3_out, and_4_out, and_5_out, and_6_out, and_7_out);
  or or_3 (out_3[0], and_8_out, and_9_out, and_10_out, and_11_out);
  or or_4 (out_3[3], and_12_out, and_13_out, and_14_out, and_15_out, and_16_out);
endmodule

module \output  (
  input  [3:0] in_1,
  output o,
  output hit
);


  assign hit = in_1[3];
  assign o = in_1[2];
endmodule
